// Logisim project ETFStudent3.circ as structural Verilog: 9 circuits, main circuit REG32_LD
module REG32_LD (
  input  [31:0] I15__0,
  input  LD,
  input  mr,
  input  CLK,
  output [31:0] A15__0
);

  // REG16_LD reg16_ld_1: pin names not known; wires that end beside it: CLK, mr, I15__0[31:16], A15__0[31:16], LD
  // REG16_LD reg16_ld_2: pin names not known; wires that end beside it: CLK, mr, I15__0[15:0], A15__0[15:0], LD

  // Notes on the sheet:
  //   __
endmodule

module KMADR (
  input  immed,
  input  memdir,
  input  regdir,
  input  regindpom,
  input  regind,
  input  memind,
  input  predec,
  output [7:0] Adr7__0
);

  assign Adr7__0 = immed ? 8'h2 : 8'bz;  // Controlled_Buffer controlled_buffer_1
  assign Adr7__0 = memdir ? 8'h4 : 8'bz;  // Controlled_Buffer controlled_buffer_2
  assign Adr7__0 = regdir ? 8'hb : 8'bz;  // Controlled_Buffer controlled_buffer_3
  assign Adr7__0 = regindpom ? 8'h10 : 8'bz;  // Controlled_Buffer controlled_buffer_4
  assign Adr7__0 = regind ? 8'ha : 8'bz;  // Controlled_Buffer controlled_buffer_5
  assign Adr7__0 = memind ? 8'h5 : 8'bz;  // Controlled_Buffer controlled_buffer_6
  assign Adr7__0 = predec ? 8'hd : 8'bz;  // Controlled_Buffer controlled_buffer_7
endmodule

module KMOPR (
  input  LD,
  input  ST,
  input  ADD,
  input  POP,
  input  PUSH,
  input  BLSSU,
  input  JEQL,
  input  JMP,
  input  JSR,
  input  RTS,
  input  RTI,
  input  HALT,
  input  INTE,
  input  INTD,
  input  ROL,
  input  BR,
  input  BLEQ,
  input  BNVF,
  input  BOVF,
  input  LOOPGRT,
  input  NOT,
  input  MUL,
  output [7:0] Adr7__0
);

  assign Adr7__0 = LD ? 8'h3a : 8'bz;  // Controlled_Buffer controlled_buffer_1
  assign Adr7__0 = ST ? 8'h3c : 8'bz;  // Controlled_Buffer controlled_buffer_2
  assign Adr7__0 = ADD ? 8'h45 : 8'bz;  // Controlled_Buffer controlled_buffer_3
  assign Adr7__0 = POP ? 8'h1b : 8'bz;  // Controlled_Buffer controlled_buffer_4
  assign Adr7__0 = PUSH ? 8'h14 : 8'bz;  // Controlled_Buffer controlled_buffer_5
  assign Adr7__0 = BLSSU ? 8'h31 : 8'bz;  // Controlled_Buffer controlled_buffer_6
  assign Adr7__0 = JEQL ? 8'h35 : 8'bz;  // Controlled_Buffer controlled_buffer_7
  assign Adr7__0 = JMP ? 8'h25 : 8'bz;  // Controlled_Buffer controlled_buffer_8
  assign Adr7__0 = JSR ? 8'h26 : 8'bz;  // Controlled_Buffer controlled_buffer_9
  assign Adr7__0 = RTS ? 8'h3 : 8'bz;  // Controlled_Buffer controlled_buffer_10
  assign Adr7__0 = RTI ? 8'ha : 8'bz;  // Controlled_Buffer controlled_buffer_11
  assign Adr7__0 = HALT ? 8'h2 : 8'bz;  // Controlled_Buffer controlled_buffer_12
  assign Adr7__0 = INTE ? 8'h10 : 8'bz;  // Controlled_Buffer controlled_buffer_13
  assign Adr7__0 = INTD ? 8'h11 : 8'bz;  // Controlled_Buffer controlled_buffer_14
  assign Adr7__0 = BR ? 8'h24 : 8'bz;  // Controlled_Buffer controlled_buffer_15
  assign Adr7__0 = ROL ? 8'h12 : 8'bz;  // Controlled_Buffer controlled_buffer_16
  assign Adr7__0 = BLEQ ? 8'h2d : 8'bz;  // Controlled_Buffer controlled_buffer_17
  assign Adr7__0 = BNVF ? 8'h2f : 8'bz;  // Controlled_Buffer controlled_buffer_18
  assign Adr7__0 = LOOPGRT ? 8'h37 : 8'bz;  // Controlled_Buffer controlled_buffer_19
  assign Adr7__0 = BOVF ? 8'h33 : 8'bz;  // Controlled_Buffer controlled_buffer_20
  assign Adr7__0 = NOT ? 8'h47 : 8'bz;  // Controlled_Buffer controlled_buffer_21
  assign Adr7__0 = MUL ? 8'h49 : 8'bz;  // Controlled_Buffer controlled_buffer_22
endmodule

module REG6_INC_LD (
  input  [5:0] I5__0,
  input  LD,
  input  INC,
  input  mr,
  input  CLK,
  output [5:0] A5__0
);

  wire reg2m_inc_ld_1_p7, reg2m_inc_ld_2_p8;

  // REG2m_INC_LD reg2m_inc_ld_1: pin names not known; wires that end beside it: CLK, mr, I5__0[5:4], A5__0[5:4], LD, INC, reg2m_inc_ld_1_p7
  // REG2m_INC_LD reg2m_inc_ld_2: pin names not known; wires that end beside it: CLK, reg2m_inc_ld_1_p7, mr, I5__0[3:2], A5__0[3:2], LD, INC, reg2m_inc_ld_2_p8
  // REG2m_INC_LD reg2m_inc_ld_3: pin names not known; wires that end beside it: CLK, reg2m_inc_ld_2_p8, mr, I5__0[1:0], A5__0[1:0], LD, INC, INC

  // Notes on the sheet:
  //   __
endmodule

module REG_FILE (
  input  in_1,
  input  in_2,
  input  in_3,
  input  [15:0] DI,
  input  [3:0] Adress,
  input  WR,
  input  CLK,
  output [15:0] DO
);

  wire A, and_1_out, and_18_out, and_20_out, mp2_16b_1_p3, mp2_16b_2_p3, mp2_16b_3_p3, PC, reg16_1_p4,
       reg16_1_p5, reg16_2_p4, reg16_2_p5, reg16_2_p6, reg16_inc_ld_1_p4, reg16_inc_ld_1_p5, reg16_ld_1_p4,
       reg16_ld_2_p4, reg16_ld_3_p4, reg16_ld_4_p4, reg16_ld_5_p4, reg16_ld_6_p4, reg16_ld_7_p4,
       reg16_ld_8_p4, reg16_ld_9_p4, reg16_ld_10_p4, reg16_ld_11_p4, reg16_ld_12_p4, reg16_ld_13_p4, RG3,
       RG4, RG5, RG6, RG7, RG8, RG9, RG10, RG11, RG12, RG13, RG14, RG15, SP;
  wire [15:0] reg16_1_p3, reg16_2_p3, reg16_inc_ld_1_p3, reg16_ld_1_p3, reg16_ld_2_p3, reg16_ld_3_p3,
       reg16_ld_4_p3, reg16_ld_5_p3, reg16_ld_6_p3, reg16_ld_7_p3, reg16_ld_8_p3, reg16_ld_9_p3,
       reg16_ld_10_p3, reg16_ld_11_p3, reg16_ld_12_p3, reg16_ld_13_p3;

  // DC4_16 dc4_16_1: pin names not known; wires that end beside it: Adress, 1'b1, A, SP, PC, RG3, RG4, RG5, RG6, RG7, RG8, RG9, RG10, RG11, RG12, RG13, RG14, RG15
  // MP2_16b mp2_16b_1: pin names not known; wires that end beside it: in_2, DI, mp2_16b_1_p3, 16'hf, 1'b1
  // REG16 reg16_1: pin names not known; wires that end beside it: CLK, mp2_16b_1_p3, reg16_1_p3, reg16_1_p4, reg16_1_p5
  assign DO = A ? reg16_1_p3 : 16'bz;  // Controlled_Buffer controlled_buffer_1
  // REG16_LD reg16_ld_1: pin names not known; wires that end beside it: CLK, DI, reg16_ld_1_p3, reg16_ld_1_p4
  assign DO = RG3 ? reg16_ld_1_p3 : 16'bz;  // Controlled_Buffer controlled_buffer_2
  // REG16_LD reg16_ld_2: pin names not known; wires that end beside it: CLK, DI, reg16_ld_2_p3, reg16_ld_2_p4
  assign DO = RG6 ? reg16_ld_2_p3 : 16'bz;  // Controlled_Buffer controlled_buffer_3
  // REG16_LD reg16_ld_3: pin names not known; wires that end beside it: CLK, DI, reg16_ld_3_p3, reg16_ld_3_p4
  assign DO = RG9 ? reg16_ld_3_p3 : 16'bz;  // Controlled_Buffer controlled_buffer_4
  // REG16_LD reg16_ld_4: pin names not known; wires that end beside it: CLK, DI, reg16_ld_4_p3, reg16_ld_4_p4
  assign DO = RG12 ? reg16_ld_4_p3 : 16'bz;  // Controlled_Buffer controlled_buffer_5
  or or_1 (reg16_1_p4, and_1_out, in_2);
  and and_1 (and_1_out, WR, A);
  and and_2 (reg16_ld_1_p4, RG3, WR);
  and and_3 (reg16_ld_2_p4, RG6, WR);
  and and_4 (reg16_ld_3_p4, RG9, WR);
  and and_5 (reg16_ld_4_p4, RG12, WR);
  and and_6 (reg16_1_p5, in_3, A);
  // REG16_LD reg16_ld_5: pin names not known; wires that end beside it: CLK, DI, reg16_ld_5_p3, reg16_ld_5_p4
  assign DO = RG4 ? reg16_ld_5_p3 : 16'bz;  // Controlled_Buffer controlled_buffer_6
  // REG16_LD reg16_ld_6: pin names not known; wires that end beside it: CLK, DI, reg16_ld_6_p3, reg16_ld_6_p4
  assign DO = RG7 ? reg16_ld_6_p3 : 16'bz;  // Controlled_Buffer controlled_buffer_7
  // REG16_LD reg16_ld_7: pin names not known; wires that end beside it: CLK, DI, reg16_ld_7_p3, reg16_ld_7_p4
  assign DO = RG10 ? reg16_ld_7_p3 : 16'bz;  // Controlled_Buffer controlled_buffer_8
  // REG16_LD reg16_ld_8: pin names not known; wires that end beside it: CLK, DI, reg16_ld_8_p3, reg16_ld_8_p4
  assign DO = RG13 ? reg16_ld_8_p3 : 16'bz;  // Controlled_Buffer controlled_buffer_9
  // REG16_LD reg16_ld_9: pin names not known; wires that end beside it: CLK, DI, reg16_ld_9_p3, reg16_ld_9_p4
  assign DO = RG15 ? reg16_ld_9_p3 : 16'bz;  // Controlled_Buffer controlled_buffer_10
  assign DO = SP ? reg16_2_p3 : 16'bz;  // Controlled_Buffer controlled_buffer_11
  and and_7 (reg16_ld_5_p4, RG4, WR);
  and and_8 (reg16_ld_6_p4, RG7, WR);
  and and_9 (reg16_ld_7_p4, RG10, WR);
  and and_10 (reg16_ld_8_p4, RG13, WR);
  and and_11 (reg16_ld_9_p4, RG15, WR);
  // MP2_16b mp2_16b_2: pin names not known; wires that end beside it: in_2, DI, mp2_16b_2_p3, 16'hf000, 1'b1
  // REG16 reg16_2: pin names not known; wires that end beside it: CLK, mp2_16b_2_p3, reg16_2_p3, reg16_2_p4, reg16_2_p5, reg16_2_p6
  and and_12 (reg16_2_p5, in_1, SP);
  // REG16_LD reg16_ld_10: pin names not known; wires that end beside it: CLK, DI, reg16_ld_10_p3, reg16_ld_10_p4
  assign DO = RG5 ? reg16_ld_10_p3 : 16'bz;  // Controlled_Buffer controlled_buffer_12
  // REG16_LD reg16_ld_11: pin names not known; wires that end beside it: CLK, DI, reg16_ld_11_p3, reg16_ld_11_p4
  assign DO = RG8 ? reg16_ld_11_p3 : 16'bz;  // Controlled_Buffer controlled_buffer_13
  // REG16_LD reg16_ld_12: pin names not known; wires that end beside it: CLK, DI, reg16_ld_12_p3, reg16_ld_12_p4
  assign DO = RG11 ? reg16_ld_12_p3 : 16'bz;  // Controlled_Buffer controlled_buffer_14
  // REG16_LD reg16_ld_13: pin names not known; wires that end beside it: CLK, DI, reg16_ld_13_p3, reg16_ld_13_p4
  assign DO = RG14 ? reg16_ld_13_p3 : 16'bz;  // Controlled_Buffer controlled_buffer_15
  and and_13 (reg16_2_p6, in_3, SP);
  and and_14 (reg16_ld_10_p4, RG5, WR);
  and and_15 (reg16_ld_11_p4, RG8, WR);
  and and_16 (reg16_ld_12_p4, RG11, WR);
  and and_17 (reg16_ld_13_p4, RG14, WR);
  or or_2 (reg16_2_p4, and_18_out, in_2);
  and and_18 (and_18_out, WR, SP);
  // MP2_16b mp2_16b_3: pin names not known; wires that end beside it: in_2, DI, mp2_16b_3_p3, 16'h1000, 1'b1
  // REG16_INC_LD reg16_inc_ld_1: pin names not known; wires that end beside it: CLK, mp2_16b_3_p3, reg16_inc_ld_1_p3, reg16_inc_ld_1_p4, reg16_inc_ld_1_p5
  assign DO = PC ? reg16_inc_ld_1_p3 : 16'bz;  // Controlled_Buffer controlled_buffer_16
  and and_19 (reg16_inc_ld_1_p5, in_1, PC);
  or or_3 (reg16_inc_ld_1_p4, and_20_out, in_2);
  and and_20 (and_20_out, WR, PC);

  // Other names for the same wires on the sheet: DEC = in_3; INC = in_1; INREG[15:0] = DI; OUTREG[15:0] = DO;
  //   RST = in_2
endmodule

module ROM32x24 (
  input  [4:0] A4__0,
  input  CS,
  output [23:0] DOUT
);

  wire [3:0] demultiplexer_1_out0, demultiplexer_1_out1;
  wire [23:0] rom_1_data, rom_2_data;

  Demultiplexer #(.width(4)) demultiplexer_1 (
    .out0(demultiplexer_1_out0), .out1(demultiplexer_1_out1), .in(A4__0[3:0]), .sel(A4__0[4]), .en(1'b1));
  ROM #(.addrWidth(4), .dataWidth(24)) rom_1 (.addr(demultiplexer_1_out0), .data(rom_1_data), .sel(CS));
  Multiplexer #(.width(24)) multiplexer_1 (.in0(rom_1_data), .in1(rom_2_data), .out(DOUT), .sel(A4__0[4]), .en(1'b1));
  ROM #(.addrWidth(4), .dataWidth(24)) rom_2 (.addr(demultiplexer_1_out1), .data(rom_2_data), .sel(CS));

  // Notes on the sheet:
  //   contents of rom_1 (hex, n*v repeats v):
  //   200 e00000 100802 80000 900 313 e00000 100807 40413 a00 512 e00000 10080c 20613 712 e00000
  //   contents of rom_2 (hex, n*v repeats v):
  //   100810 10900 c100 a100
endmodule

module ROM32x24_ADDR (
  input  [4:0] A4__0,
  input  CS,
  output [23:0] DOUT
);

  wire [3:0] demultiplexer_1_out0, demultiplexer_1_out1;
  wire [23:0] rom_1_data, rom_2_data;

  Demultiplexer #(.width(4)) demultiplexer_1 (
    .out0(demultiplexer_1_out0), .out1(demultiplexer_1_out1), .in(A4__0[3:0]), .sel(A4__0[4]), .en(1'b1));
  ROM #(.addrWidth(4), .dataWidth(24)) rom_1 (.addr(demultiplexer_1_out0), .data(rom_1_data), .sel(CS));
  Multiplexer #(.width(24)) multiplexer_1 (.in0(rom_1_data), .in1(rom_2_data), .out(DOUT), .sel(A4__0[4]), .en(1'b1));
  ROM #(.addrWidth(4), .dataWidth(24)) rom_2 (.addr(demultiplexer_1_out1), .data(rom_2_data), .sel(CS));

  // Notes on the sheet:
  //   contents of rom_1 (hex, n*v repeats v):
  //   200 400 316 c00116 300111 300000 80506 450000 80508 340111 208111 316 c28116 c28000 c60000 32c111
  //   contents of rom_2 (hex, n*v repeats v):
  //   368111 316 80512 850000 80514 440000 3100
endmodule

module ROM_EXEC (
  input  [7:0] ADRESA,
  input  CS,
  output [31:0] out_3,
  output [7:0] out_4
);

  ROM rom_1 (.addr(ADRESA), .data(out_4), .sel(CS));
  ROM #(.dataWidth(32)) rom_2 (.addr(ADRESA), .data(out_3), .sel(CS));

  // Notes on the sheet:
  //   contents of rom_1 (hex, n*v repeats v):
  //   0 0 54 0 0 5 0 7 0 54 0 0 c 0 e 3 54 54 0 54 0 0 16 0 0 19 54 0 0 1d 0 0 20 0 0 54 54 54 0 0 28 0 0
  //   2b 25 54 24 54 24 54 24 54 24 54 24 0 54 25 0 54 54 43 0 3f 0 41 54 0 54 0 54 0 54
  //   contents of rom_2 (hex, n*v repeats v):
  //   4 2 10000001 c000000 e000000 1000003 a600000 1000003 a00000 180001 c000000 e000000 1000003 a07c000
  //   1000003 2001 2001 2001 101000 10001 a000400 1000200 103 a000400 1200200 103 1 c000000 e000000
  //   1000003 600000 a000000 1000003 a00000 100000 18001 180801 181801 a000400 1080200 103 a000400 1280200
  //   103 1 5 1 5 1 5 1 5 1 5 1 4020000 18005 1 100000 18001 6 7 1000200 103 21200200 103 1 40c00000
  //   100081 121000 18001 101000 18001 40 8*20 101000 8000 80000011
endmodule

module ROM_INTR (
  input  [7:0] ADRESA,
  input  CS,
  output [29:0] out_3
);

  ROM #(.dataWidth(30)) rom_1 (.addr(ADRESA), .data(out_3), .sel(CS));

  // Notes on the sheet:
  //   contents of rom_1 (hex, n*v repeats v):
  //   200 315 29000000 14800000 400404 29000000 14a00000 400407 29000000 4900000 40040a 29000000 4b00000
  //   40040d 80000 8360000 4000410 218000 4000412 204000 12000000 3100
endmodule
