// Logisim project main3 - Copy.circ as structural Verilog: 8 circuits, main circuit COMPUTER
module COMPUTER (
);

  wire BTN_RST_out, CLK, cpu_1_inta, interrupt_interface_4_1_p4, interrupt_interface_4_1_p5,
       interrupt_interface_4_1_p6, interrupt_interface_4_1_p7, pull_resistor_1_node, pull_resistor_6_node,
       ram_1_out_8, rst;
  wire [1:0] cpu_1_uext1__0;
  wire [3:0] interrupt_interface_4_1_p1;
  wire [7:0] pull_resistor_4_node, ram_1_out_7;
  wire [15:0] pull_resistor_2_node;

  Button BTN_RST (.out(BTN_RST_out));
  Clock u_CLK (.out(CLK));
  // RisingEdge risingedge_1: pin names not known; wires that end beside it: BTN_RST_out, CLK, rst
  RAM ram_1 (
    .in_1(pull_resistor_2_node), .in_2(CLK), .in_3(pull_resistor_4_node), .in_4(pull_resistor_1_node),
    .in_5(pull_resistor_6_node), .in_6(rst), .out_7(ram_1_out_7), .out_8(ram_1_out_8));
  Pull_Resistor pull_resistor_1 (.node(pull_resistor_1_node));
  Pull_Resistor pull_resistor_2 (.node(pull_resistor_2_node));
  Pull_Resistor pull_resistor_3 (.node(ram_1_out_7));
  Pull_Resistor pull_resistor_4 (.node(pull_resistor_4_node));
  Pull_Resistor pull_resistor_5 (.node(ram_1_out_8));
  Pull_Resistor pull_resistor_6 (.node(pull_resistor_6_node));
  CPU cpu_1 (
    .in_1(rst), .in_2(CLK), .in_3(ram_1_out_8), .in_4(ram_1_out_7), .ABUS(pull_resistor_2_node),
    .DOUTBUS(pull_resistor_4_node), .out_8(pull_resistor_1_node), .out_9(pull_resistor_6_node),
    .inta(cpu_1_inta), .intr3__0(interrupt_interface_4_1_p1), .UEXT1__0(cpu_1_uext1__0));
  // INTERRUPT_INTERFACE_4 interrupt_interface_4_1: pin names not known; wires that end beside it: interrupt_interface_4_1_p1, cpu_1_inta, cpu_1_uext1__0, interrupt_interface_4_1_p4, interrupt_interface_4_1_p5, interrupt_interface_4_1_p6, interrupt_interface_4_1_p7, CLK
  Button BTN_INTR3 (.out(interrupt_interface_4_1_p4));
  Button BTN_INTR2 (.out(interrupt_interface_4_1_p5));
  Button BTN_INTR1 (.out(interrupt_interface_4_1_p6));
  Button BTN_INTR0 (.out(interrupt_interface_4_1_p7));
endmodule

module CPU (
  input  in_1,
  input  in_2,
  input  in_3,
  input  [7:0] in_4,
  input  [3:0] intr3__0,
  output [15:0] ABUS,
  output [7:0] DOUTBUS,
  output out_8,
  output out_9,
  output inta,
  output [1:0] UEXT1__0
);

  wire [3:0] common_1_phaseffbus;
  wire [5:0] common_1_addrbus, pull_resistor_2_node;
  wire [7:0] ALU, PSW;
  wire [9:0] pull_resistor_6_node;
  wire [14:0] pull_resistor_7_node;
  wire [15:0] A, B, INTRADDR;
  wire [19:0] pull_resistor_5_node;
  wire [31:0] common_1_instrucbus;

  COMMON common_1 (
    .CLK(in_2), .RST(in_1), .DIN(in_4), .CMEMBUS(pull_resistor_7_node), .MAR(ABUS), .MDR(DOUTBUS),
    .PHASEFFBUS(common_1_phaseffbus), .INSTRUCBUS(common_1_instrucbus), .ADDRBUS(common_1_addrbus),
    .PSW(PSW), .CREGBUS(pull_resistor_5_node), .CFFBUS(pull_resistor_6_node), .B(B), .A(A),
    .CPSW(pull_resistor_2_node), .ALU(ALU), .IVTPPDSP(INTRADDR));
  Pull_Resistor pull_resistor_1 (.node(common_1_phaseffbus));
  Pull_Resistor pull_resistor_2 (.node(pull_resistor_2_node));
  Pull_Resistor pull_resistor_3 (.node(common_1_instrucbus));
  Pull_Resistor pull_resistor_4 (.node(common_1_addrbus));
  Pull_Resistor pull_resistor_5 (.node(pull_resistor_5_node));
  Pull_Resistor pull_resistor_6 (.node(pull_resistor_6_node));
  Pull_Resistor pull_resistor_7 (.node(pull_resistor_7_node));
  FETCH fetch_1 (
    .in_1(in_1), .in_2(in_2), .in_3(in_3), .PHASEFFBUS(common_1_phaseffbus),
    .INSTRUCBUS(common_1_instrucbus), .ADDRBUS(common_1_addrbus), .PSW(PSW), .rdMEM(out_9),
    .CMEMBUS(pull_resistor_7_node), .CFFBUS(pull_resistor_6_node), .CREGBUS(pull_resistor_5_node));
  ADDR addr_1 (
    .in_1(in_1), .in_2(in_2), .in_3(in_3), .PHASEFFBUS(common_1_phaseffbus),
    .INSTRUCBUS(common_1_instrucbus), .ADDRBUS(common_1_addrbus), .rdMEM(out_9),
    .CMEMBUS(pull_resistor_7_node), .CFFBUS(pull_resistor_6_node), .CREGBUS(pull_resistor_5_node));
  EXEC exec_1 (
    .in_1(in_1), .in_2(in_2), .in_3(in_3), .B(B), .PHASEFFBUS(common_1_phaseffbus),
    .INSTRUCBUS(common_1_instrucbus), .ADDRBUS(common_1_addrbus), .PSW(PSW), .A(A), .ALU(ALU),
    .CMEMBUS(pull_resistor_7_node), .CFFBUS(pull_resistor_6_node), .CREGBUS(pull_resistor_5_node),
    .CPSW(pull_resistor_2_node), .rdMEM(out_9), .wrMEM(out_8));

  // Other names for the same wires on the sheet: CLK = in_2; DIN7__0[7:0] = in_4; FCBUS = in_3; MAR[15:0] = ABUS;
  //   MDR[7:0] = DOUTBUS; RD = out_9; rst = in_1; WR = out_8
endmodule

module COMMON (
  input  CLK,
  input  RST,
  input  [7:0] DIN,
  input  [15:0] A,
  input  [7:0] ALU,
  input  [15:0] IVTPPDSP,
  input  [14:0] CMEMBUS,
  input  [9:0] CFFBUS,
  input  [19:0] CREGBUS,
  input  [5:0] CPSW,
  output [15:0] MAR,
  output [7:0] MDR,
  output [3:0] PHASEFFBUS,
  output [31:0] INSTRUCBUS,
  output [5:0] ADDRBUS,
  output [7:0] PSW,
  output [15:0] B
);

  wire adrinst, bezadrinst, branchinst, clB, dc4_16_1_p3, dc4_16_1_p4, dc4_16_1_p5, decB, decSP, incB, incSP,
       jmpinst, ldDWH, ldDWL, mp2_16b_1_p3, mp4_16b_1_p5, mp4_16b_2_p5, mp8_8b_1_p7, mp8_16b_1_p7,
       mp8_16b_1_p8, mxGPR0, mxMDR0, mxMDR1, mxMDR2, mxPC0, mxPC1, not_1_out, not_4_out, reg16_inc_ld_2_p4,
       rsff_2_p4, rsff_3_p4, rsff_5_p4, shrB, wrGPR;
  wire [3:0] IR27__24;
  wire [7:0] A7__0, DWH7__0, DWL7__0, gpr16x16_1_p1, IR7__0, IR15__8, IR23__16;
  wire [7:4] IR31__24;
  wire [15:0] ADDPCREL15__0, GPR15__0, mp8_8b_1_p8, PC15__0, SP15__0;

  // REG8_LD reg8_ld_1: pin names not known; wires that end beside it: CLK, MDR, IR23__16, CREGBUS[2]
  // MP8_16b mp8_16b_1: pin names not known; wires that end beside it: CMEMBUS[5], CMEMBUS[6], CMEMBUS[7], PC15__0, {IR15__8, IR7__0}, GPR15__0, mp8_16b_1_p7, mp8_16b_1_p8, mp8_16b_1_p8, 1'b1
  // REG16_INC_LD reg16_inc_ld_1: pin names not known; wires that end beside it: CLK, mp8_16b_1_p7, MAR, CMEMBUS[0], CMEMBUS[1]
  // REG8_LD reg8_ld_2: pin names not known; wires that end beside it: CLK, MDR, {IR31__24, IR27__24}, CREGBUS[3]
  // DC4_16 dc4_16_1: pin names not known; wires that end beside it: IR31__24, PSW[0], dc4_16_1_p3, dc4_16_1_p4, dc4_16_1_p5, adrinst, jmpinst, bezadrinst, branchinst, dc4_16_1_p3, dc4_16_1_p4, dc4_16_1_p5
  // DC4_16 dc4_16_2: pin names not known; wires that end beside it: IR27__24, adrinst, INSTRUCBUS[14], INSTRUCBUS[15], INSTRUCBUS[16], INSTRUCBUS[17], INSTRUCBUS[18], INSTRUCBUS[19], INSTRUCBUS[20]
  // MP4_16b mp4_16b_1: pin names not known; wires that end beside it: CREGBUS[6], CREGBUS[5], {{8{1'b0}}, MDR}, {IR15__8, IR7__0}, mp4_16b_1_p5, mp4_16b_1_p5, GPR15__0, {16{1'b0}}, 1'b1
  // REG16 reg16_1: pin names not known; wires that end beside it: clB, shrB, CLK, B, CREGBUS[4], incB, decB
  // Probe on B
  // REG8_LD reg8_ld_3: pin names not known; wires that end beside it: CLK, MDR, IR15__8, CREGBUS[1]
  // ADD16 add16_1: pin names not known; wires that end beside it: {{9{IR23__16[7]}}, IR23__16[6:0]}, ADDPCREL15__0, PC15__0
  // MP8_8b mp8_8b_1: pin names not known; wires that end beside it: mxMDR2, mxMDR1, mxMDR0, DIN, A7__0, PC15__0[15:8], mp8_8b_1_p7, mp8_8b_1_p8, PC15__0[7:0], mp8_8b_1_p8[15:8], mp8_8b_1_p8[7:0], 1'b1
  // Probe on mp8_8b_1_p7
  // REG8_LD reg8_ld_4: pin names not known; wires that end beside it: CLK, mp8_8b_1_p7, MDR, CMEMBUS[2]
  // DC4_16 dc4_16_3: pin names not known; wires that end beside it: IR27__24, bezadrinst, INSTRUCBUS[0], INSTRUCBUS[1], INSTRUCBUS[2], INSTRUCBUS[3], INSTRUCBUS[4], INSTRUCBUS[5], INSTRUCBUS[6], INSTRUCBUS[7], INSTRUCBUS[8], INSTRUCBUS[9]
  // DC4_16 dc4_16_4: pin names not known; wires that end beside it: IR27__24, jmpinst, INSTRUCBUS[21], INSTRUCBUS[22]
  // REG8_LD reg8_ld_5: pin names not known; wires that end beside it: CLK, MDR, IR7__0, CREGBUS[0]
  // REG8_LD reg8_ld_6: pin names not known; wires that end beside it: CLK, MDR, DWH7__0, ldDWH
  // REG8_LD reg8_ld_7: pin names not known; wires that end beside it: CLK, MDR, DWL7__0, ldDWL
  // MP4_16b mp4_16b_2: pin names not known; wires that end beside it: mxPC1, mxPC0, {IR15__8, IR7__0}, {DWH7__0, DWL7__0}, mp4_16b_2_p5, 1'b1
  // DC2_4 dc2_4_1: pin names not known; wires that end beside it: IR27__24[3:2], branchinst, INSTRUCBUS[10], INSTRUCBUS[11], INSTRUCBUS[12], INSTRUCBUS[13]
  // DC4_16 dc4_16_5: pin names not known; wires that end beside it: IR23__16[7:4], adrinst, ADDRBUS[0], ADDRBUS[1], ADDRBUS[2], ADDRBUS[3], ADDRBUS[4], ADDRBUS[5]
  // REG16 reg16_2: pin names not known; wires that end beside it: CLK, 16'hf000, SP15__0, RST, incSP, decSP
  not not_1 (not_1_out, RST);
  // RSFF rsff_1: pin names not known; wires that end beside it: CFFBUS[1], CLK, CFFBUS[0], not_1_out, PHASEFFBUS[0]
  // MP2_16b mp2_16b_1: pin names not known; wires that end beside it: RST, mp4_16b_2_p5, mp2_16b_1_p3, 16'h1000, 1'b1
  // REG16_INC_LD reg16_inc_ld_2: pin names not known; wires that end beside it: CLK, mp2_16b_1_p3, PC15__0, reg16_inc_ld_2_p4, CMEMBUS[4]
  or or_1 (reg16_inc_ld_2_p4, CMEMBUS[3], RST);
  // RSFF rsff_2: pin names not known; wires that end beside it: CFFBUS[3], CLK, CFFBUS[2], rsff_2_p4, PHASEFFBUS[1]
  not not_2 (rsff_2_p4, RST);
  // RSFF rsff_3: pin names not known; wires that end beside it: CFFBUS[5], CLK, CFFBUS[4], rsff_3_p4, PHASEFFBUS[2]
  not not_3 (rsff_3_p4, RST);
  // GPR16x16 gpr16x16_1: pin names not known; wires that end beside it: gpr16x16_1_p1, IR23__16[3:0], CLK, {gpr16x16_1_p1, B[7:0]}, GPR15__0, wrGPR
  not not_4 (not_4_out, RST);
  // RSFF rsff_4: pin names not known; wires that end beside it: CFFBUS[8], CLK, not_4_out, PSW[0]
  // RSFF rsff_5: pin names not known; wires that end beside it: CFFBUS[7], CLK, CFFBUS[6], rsff_5_p4, PHASEFFBUS[3]
  not not_5 (rsff_5_p4, RST);
  // MP2_16b mp2_16b_2: pin names not known; wires that end beside it: mxGPR0, B, A, 1'b1

  assign CPSW[0] = CFFBUS[8];

  // Other names for the same wires on the sheet: MDR7__0[7:0] = MDR; B7__0[7:0] = B[7:0]; B15__0[15:0] = B;
  //   A15__0[15:0] = A; immed = ADDRBUS[0]; memdir = ADDRBUS[1]; regdir = ADDRBUS[2]; regind = ADDRBUS[3];
  //   brpom = ADDRBUS[4]; bxpom = ADDRBUS[5]; ALU7__0[7:0] = ALU; stariji[7:0] = B[15:8]; stFETCH = CFFBUS[0];
  //   clFETCH = CFFBUS[1]; stADDR = CFFBUS[2]; clADDR = CFFBUS[3]; stEXEC = CFFBUS[4]; clEXEC = CFFBUS[5];
  //   stINTR = CFFBUS[6]; clINTR = CFFBUS[7]; ldMAR = CMEMBUS[0]; incMAR = CMEMBUS[1]; ldMDR = CMEMBUS[2];
  //   ldPC = CMEMBUS[3]; incPC = CMEMBUS[4]; mxMAR2 = CMEMBUS[5]; mxMAR1 = CMEMBUS[6]; mxMAR0 = CMEMBUS[7];
  //   clPSWSTART = CFFBUS[8]; ldIR7__0 = CREGBUS[0]; ldIR15__8 = CREGBUS[1]; ldIR23__16 = CREGBUS[2];
  //   ldIR31__24 = CREGBUS[3]; ldB = CREGBUS[4]; mxB0 = CREGBUS[5]; mxB1 = CREGBUS[6]; Din7__0[7:0] = DIN;
  //   ENTRADDR15__0[15:0] = IVTPPDSP; HALT = INSTRUCBUS[0]; RTS = INSTRUCBUS[1]; RTI = INSTRUCBUS[2];
  //   INTE = INSTRUCBUS[3]; INTD = INSTRUCBUS[4]; PUSH = INSTRUCBUS[5]; POP = INSTRUCBUS[6]; STBR = INSTRUCBUS[7];
  //   STXR = INSTRUCBUS[8]; STAR = INSTRUCBUS[9]; BNEQ = INSTRUCBUS[10]; BOVF = INSTRUCBUS[11]; JNNG = INSTRUCBUS[12];
  //   JGRT = INSTRUCBUS[13]; LD = INSTRUCBUS[14]; ST = INSTRUCBUS[15]; INC = INSTRUCBUS[16]; SUB = INSTRUCBUS[17];
  //   TST = INSTRUCBUS[18]; STRCPY = INSTRUCBUS[19]; JADR = INSTRUCBUS[20]; JMP = INSTRUCBUS[21];
  //   JSR = INSTRUCBUS[22]; IR31__24[3:0] = IR27__24; MAR15__0[15:0] = MAR; FETCH = PHASEFFBUS[0];
  //   ADDR = PHASEFFBUS[1]; EXEC = PHASEFFBUS[2]; INTR = PHASEFFBUS[3]; PSW7__0[7:0] = PSW; PSWSTART = PSW[0]

  // Notes on the sheet:
  //   Sabirac
  //   Sabirac
  //   Instrukcijski registar
  //   Pomocni registri
  //   MAR
  //   Dekoderi za prepoznavanje instrukcije na osnovu sadrzaja registra IR23..16
  //   MDR
  //   SP
  //   PC
  //   Dekoderi za prepoznavanje nacina adresiranja
  //   FF za pokretanje FETCH, ADDR, EXEC i INTR faze izvršavanja instrukcije
  //   Registarski fajl
  //   Programska statusna reč (PSW)
endmodule

module FETCH (
  input  in_1,
  input  in_2,
  input  in_3,
  input  [3:0] PHASEFFBUS,
  input  [31:0] INSTRUCBUS,
  input  [5:0] ADDRBUS,
  input  [7:0] PSW,
  output [14:0] CMEMBUS,
  output [9:0] CFFBUS,
  output [19:0] CREGBUS,
  output rdMEM
);

  wire addr2, addr3, addr4, addr_t, and_4_out, and_5_out, and_6_out, and_7_out, and_8_out, and_9_out,
       and_10_out, and_11_out, bezadr1, bradr1, bradr2, bradr3, bradr4, brbezadr1, brcnd, brjmp2, brjmp3,
       brnotfcmem, bruncnd, clFETCH, incPC, jmp2, jmp3, ldIR7__0, ldIR15__8, ldIR23__16, ldIR31__24, ldMAR,
       ldMDR, not_1_out, not_3_out, not_4_out, not_5_out, notPSWSTandFETCH, or_4_out, or_6_out, or_7_out,
       or_8_out, rdMEM_t, reg5_cl_inc_ld_1_p5, reg5_cl_inc_ld_1_p6, stADDR, stEXEC;
  wire [4:0] reg5_cl_inc_ld_1_p4;
  wire [19:11] reg5_cl_inc_ld_1_p3;

  not not_1 (not_1_out, in_1);
  // REG5_CL_INC_LD reg5_cl_inc_ld_1: pin names not known; wires that end beside it: in_2, not_1_out, reg5_cl_inc_ld_1_p3[19:15], reg5_cl_inc_ld_1_p4, reg5_cl_inc_ld_1_p5, reg5_cl_inc_ld_1_p6
  or or_1 (jmp2, INSTRUCBUS[10], INSTRUCBUS[11]);
  or or_2 (jmp3, INSTRUCBUS[12], INSTRUCBUS[21], INSTRUCBUS[22], INSTRUCBUS[13]);
  or or_3 (reg5_cl_inc_ld_1_p5, bruncnd, brcnd);
  not not_2 (reg5_cl_inc_ld_1_p6, reg5_cl_inc_ld_1_p5);
  or or_4 (or_4_out, ADDRBUS[2], ADDRBUS[3]);
  ROM #(.addrWidth(5), .dataWidth(20)) rom_1 (
    .addr(reg5_cl_inc_ld_1_p4),
    .data({reg5_cl_inc_ld_1_p3, stEXEC, stADDR, clFETCH, ldIR7__0, ldIR15__8, ldIR23__16, ldIR31__24, ldMDR, rdMEM_t, incPC, ldMAR}),
    .sel(1'b1));
  and and_1 (addr2, addr_t, or_4_out);
  or or_5 (addr_t, INSTRUCBUS[14], INSTRUCBUS[15], INSTRUCBUS[16], INSTRUCBUS[17], INSTRUCBUS[18], INSTRUCBUS[19], INSTRUCBUS[20]);
  // DC4_16 dc4_16_1: pin names not known; wires that end beside it: reg5_cl_inc_ld_1_p3[14:11], 1'b1, brjmp2, bruncnd, notPSWSTandFETCH, brbezadr1, bradr1, bradr2, bradr3, brjmp3, bradr4, brnotfcmem
  or or_6 (or_6_out, ADDRBUS[0], ADDRBUS[1]);
  or or_7 (or_7_out, ADDRBUS[4], ADDRBUS[5]);
  and and_2 (addr4, addr_t, or_6_out);
  and and_3 (addr3, addr_t, or_7_out);
  not not_3 (not_3_out, PHASEFFBUS[0]);
  not not_4 (not_4_out, PSW[0]);
  or or_8 (or_8_out, not_3_out, not_4_out);
  not not_5 (not_5_out, in_3);
  or or_9 (bezadr1, INSTRUCBUS[0], INSTRUCBUS[1], INSTRUCBUS[2], INSTRUCBUS[3], INSTRUCBUS[4], INSTRUCBUS[5], INSTRUCBUS[6], INSTRUCBUS[7], INSTRUCBUS[8], INSTRUCBUS[9]);
  and and_4 (and_4_out, or_8_out, notPSWSTandFETCH);
  and and_5 (and_5_out, brbezadr1, bezadr1);
  and and_6 (and_6_out, brjmp2, jmp2);
  and and_7 (and_7_out, bradr2, addr2);
  and and_8 (and_8_out, brjmp3, jmp3);
  and and_9 (and_9_out, brnotfcmem, not_5_out);
  and and_10 (and_10_out, bradr3, addr3);
  and and_11 (and_11_out, bradr4, addr4);
  or or_10 (brcnd, and_4_out, and_5_out, and_6_out, and_7_out, and_8_out, and_9_out, and_10_out, and_11_out);
  assign CMEMBUS[0] = ldMAR ? 1'b1 : 1'bz;  // Controlled_Buffer controlled_buffer_1
  assign CMEMBUS[2] = ldMDR ? 1'b1 : 1'bz;  // Controlled_Buffer controlled_buffer_2
  assign CMEMBUS[4] = incPC ? 1'b1 : 1'bz;  // Controlled_Buffer controlled_buffer_3
  assign CFFBUS[1] = clFETCH ? 1'b1 : 1'bz;  // Controlled_Buffer controlled_buffer_4
  assign CFFBUS[2] = stADDR ? 1'b1 : 1'bz;  // Controlled_Buffer controlled_buffer_5
  assign CFFBUS[4] = stEXEC ? 1'b1 : 1'bz;  // Controlled_Buffer controlled_buffer_6
  assign CREGBUS[0] = ldIR7__0 ? 1'b1 : 1'bz;  // Controlled_Buffer controlled_buffer_7
  assign CREGBUS[1] = ldIR15__8 ? 1'b1 : 1'bz;  // Controlled_Buffer controlled_buffer_8
  assign CREGBUS[2] = ldIR23__16 ? 1'b1 : 1'bz;  // Controlled_Buffer controlled_buffer_9
  assign CREGBUS[3] = ldIR31__24 ? 1'b1 : 1'bz;  // Controlled_Buffer controlled_buffer_10
  assign rdMEM = rdMEM_t ? 1'b1 : 1'bz;  // Controlled_Buffer controlled_buffer_11

  // Other names for the same wires on the sheet: immed = ADDRBUS[0]; memdir = ADDRBUS[1]; regdir = ADDRBUS[2];
  //   regind = ADDRBUS[3]; brpom = ADDRBUS[4]; bxpom = ADDRBUS[5]; CLK = in_2; FCBUS = in_3; HALT = INSTRUCBUS[0];
  //   RTS = INSTRUCBUS[1]; RTI = INSTRUCBUS[2]; INTE = INSTRUCBUS[3]; INTD = INSTRUCBUS[4]; PUSH = INSTRUCBUS[5];
  //   POP = INSTRUCBUS[6]; STBR = INSTRUCBUS[7]; STXR = INSTRUCBUS[8]; STAR = INSTRUCBUS[9]; BNEQ = INSTRUCBUS[10];
  //   BOVF = INSTRUCBUS[11]; JNNG = INSTRUCBUS[12]; JGRT = INSTRUCBUS[13]; LD = INSTRUCBUS[14]; ST = INSTRUCBUS[15];
  //   INC = INSTRUCBUS[16]; SUB = INSTRUCBUS[17]; TST = INSTRUCBUS[18]; STRCPY = INSTRUCBUS[19];
  //   JADR = INSTRUCBUS[20]; JMP = INSTRUCBUS[21]; JSR = INSTRUCBUS[22]; FETCH = PHASEFFBUS[0]; ADDR = PHASEFFBUS[1];
  //   EXEC = PHASEFFBUS[2]; INTR = PHASEFFBUS[3]; PSWSTART = PSW[0]; rst = in_1

  // Notes on the sheet:
  //   Operaciona jedinica
  //   Kontrolna jedinica
  //   contents of rom_1 (hex, n*v repeats v):
  //   1000 3 1500c 10 9a000 a1800 3 3d00c 20 a3000 9a800 3 6500c 40 a3800 9c000 3 8d00c 80 300 500
endmodule

module ADDR (
  input  in_1,
  input  in_2,
  input  in_3,
  input  [3:0] PHASEFFBUS,
  input  [31:0] INSTRUCBUS,
  input  [5:0] ADDRBUS,
  output [14:0] CMEMBUS,
  output [9:0] CFFBUS,
  output [19:0] CREGBUS,
  output rdMEM
);

  wire and_1_out, and_2_out, and_3_out, bradr, brcnd, brnotADDR, brnotFCBUS, brST_STRFIND, bruncnd, clADDR,
       ldB, ldMAR, ldMRD, mxB0, mxB1, mxMAR0, mxMAR1, not_1_out, not_3_out, not_4_out, rdMEM_t,
       reg5_cl_inc_ld_1_p6, reg5_cl_inc_ld_1_p7, stEXEC;
  wire [4:0] kmadr_1_p5, multiplexer_1_out, reg5_cl_inc_ld_1_p5, rom_1_data_2;
  wire [17:10] rom_1_data;

  // KMADR kmadr_1: pin names not known; wires that end beside it: ADDRBUS[0], ADDRBUS[1], ADDRBUS[2], ADDRBUS[3], kmadr_1_p5, ADDRBUS[4], ADDRBUS[5], ADDRBUS[5]
  Multiplexer #(.width(5), .enable("false")) multiplexer_1 (
    .in0(rom_1_data[17:13]), .in1(kmadr_1_p5), .out(multiplexer_1_out), .sel(bradr));
  not not_1 (not_1_out, in_1);
  // REG5_CL_INC_LD reg5_cl_inc_ld_1: pin names not known; wires that end beside it: 1'b0, in_2, not_1_out, multiplexer_1_out, reg5_cl_inc_ld_1_p5, reg5_cl_inc_ld_1_p6, reg5_cl_inc_ld_1_p7
  not not_2 (reg5_cl_inc_ld_1_p7, reg5_cl_inc_ld_1_p6);
  or or_1 (reg5_cl_inc_ld_1_p6, bruncnd, brcnd, bradr);
  ROM #(.addrWidth(5), .dataWidth(23)) rom_1 (
    .addr(reg5_cl_inc_ld_1_p5),
    .data({rom_1_data_2, rom_1_data, stEXEC, clADDR, ldMRD, rdMEM_t, mxMAR1, mxB1, mxMAR0, ldMAR, mxB0, ldB}),
    .sel(1'b1));
  // DC3_8 dc3_8_1: pin names not known; wires that end beside it: rom_1_data[12:10], 1'b1, bruncnd, brnotADDR, brST_STRFIND, brnotFCBUS, bradr
  not not_3 (not_3_out, PHASEFFBUS[1]);
  not not_4 (not_4_out, in_3);
  and and_1 (and_1_out, not_3_out, brnotADDR);
  and and_2 (and_2_out, INSTRUCBUS[15], brST_STRFIND);
  and and_3 (and_3_out, brnotFCBUS, not_4_out);
  or or_2 (brcnd, and_1_out, and_2_out, and_3_out);
  assign CMEMBUS[0] = ldMAR ? 1'b1 : 1'bz;  // Controlled_Buffer controlled_buffer_1
  assign CMEMBUS[6] = mxMAR1 ? 1'b1 : 1'bz;  // Controlled_Buffer controlled_buffer_2
  assign CMEMBUS[7] = mxMAR0 ? 1'b1 : 1'bz;  // Controlled_Buffer controlled_buffer_3
  assign CFFBUS[3] = clADDR ? 1'b1 : 1'bz;  // Controlled_Buffer controlled_buffer_4
  assign CFFBUS[4] = stEXEC ? 1'b1 : 1'bz;  // Controlled_Buffer controlled_buffer_5
  assign CREGBUS[4] = ldB ? 1'b1 : 1'bz;  // Controlled_Buffer controlled_buffer_6
  assign CREGBUS[5] = mxB0 ? 1'b1 : 1'bz;  // Controlled_Buffer controlled_buffer_7
  assign CREGBUS[6] = mxB1 ? 1'b1 : 1'bz;  // Controlled_Buffer controlled_buffer_8
  assign rdMEM = rdMEM_t ? 1'b1 : 1'bz;  // Controlled_Buffer controlled_buffer_9

  // Other names for the same wires on the sheet: immed = ADDRBUS[0]; memdir = ADDRBUS[1]; regdir = ADDRBUS[2];
  //   regind = ADDRBUS[3]; brpom = ADDRBUS[4]; bxpom = ADDRBUS[5]; CLK = in_2; FCBUS = in_3; HALT = INSTRUCBUS[0];
  //   RTS = INSTRUCBUS[1]; RTI = INSTRUCBUS[2]; INTE = INSTRUCBUS[3]; INTD = INSTRUCBUS[4]; PUSH = INSTRUCBUS[5];
  //   POP = INSTRUCBUS[6]; STBR = INSTRUCBUS[7]; STXR = INSTRUCBUS[8]; STAR = INSTRUCBUS[9]; BNEQ = INSTRUCBUS[10];
  //   BOVF = INSTRUCBUS[11]; JNNG = INSTRUCBUS[12]; JGRT = INSTRUCBUS[13]; LD = INSTRUCBUS[14]; ST = INSTRUCBUS[15];
  //   INC = INSTRUCBUS[16]; SUB = INSTRUCBUS[17]; TST = INSTRUCBUS[18]; STRCPY = INSTRUCBUS[19];
  //   JADR = INSTRUCBUS[20]; JMP = INSTRUCBUS[21]; JSR = INSTRUCBUS[22]; FETCH = PHASEFFBUS[0]; ADDR = PHASEFFBUS[1];
  //   EXEC = PHASEFFBUS[2]; INTR = PHASEFFBUS[3]; rst = in_1

  // Notes on the sheet:
  //   Operaciona jedinica
  //   Upravljacka jedinica
  //   contents of rom_1 (hex, n*v repeats v):
  //   800 1400 10403 1040c c411 24 d0c0 1 700
endmodule

module EXEC (
  input  in_1,
  input  in_2,
  input  in_3,
  input  [15:0] B,
  input  [31:0] INSTRUCBUS,
  input  [5:0] ADDRBUS,
  input  [7:0] PSW,
  input  [3:0] PHASEFFBUS,
  output [15:0] A,
  output [7:0] ALU,
  output [14:0] CMEMBUS,
  output [9:0] CFFBUS,
  output [19:0] CREGBUS,
  output [5:0] CPSW,
  output rdMEM,
  output wrMEM
);

  wire add, and_1_out, and_2_out, and_3_out, and_4_out, and_5_out, and_6_out, brbrorjmp, brcnd, brmul,
       brnotEXEC, brnotFCBUS, brnotStopLoop, brorjmp, brPOPPSW, brregdir, bruncd, clB, clEXEC, clPSWSTART,
       Cout, decB, decMAR, decSP, equal, incA, incB, incMAR, incSP, ldA, ldB, ldBR, ldC, ldDWH, ldDWL, ldI,
       ldIVTP, ldMAR, ldMDR, ldPC, ldSTART, ldV, MDRis0, mp8_16b_1_p7, mx0, mxA0, mxA1, mxB0, mxB1, mxMAR2,
       mxMDR0, mxMDR1, mxMDR2, mxPC0, mxPC1, mxRO0, not_1_out, not_2_out, not_3_out, not_4_out, not_5_out,
       \or , or_1_out, POPPSW, rdMEM_t, regdir, shrB, stINTR, stopLoop, wrGPR, wrMEM_t;
  wire [3:0] dc4_16_1_p1;
  wire [6:0] counter_1_q, kmopr_1_p1, multiplexer_1_out;
  wire [7:0] A7__0, B7__0, BR7__0, SUB7__0;
  wire [15:0] MDR7__0, SUB15__0;
  wire [31:25] rom_1_data;

  // MP8_16b mp8_16b_1: pin names not known; wires that end beside it: 1'b0, mxA1, mxA0, B, MDR7__0, SUB15__0, mp8_16b_1_p7, 1'b1
  not not_1 (not_1_out, in_1);
  // REG16m_INC_LD reg16m_inc_ld_1: pin names not known; wires that end beside it: in_2, not_1_out, mp8_16b_1_p7, A, ldA, incA
  or or_1 (or_1_out, bruncd, brcnd, brmul);
  // DC4_16 dc4_16_1: pin names not known; wires that end beside it: dc4_16_1_p1, bruncd, brnotEXEC, brmul, brregdir, brnotFCBUS, brnotStopLoop, brbrorjmp, brPOPPSW
  Multiplexer #(.width(7), .enable("false")) multiplexer_1 (
    .in0(rom_1_data), .in1(kmopr_1_p1), .out(multiplexer_1_out), .sel(brmul));
  Counter #(.width(7), .max('h7f)) counter_1 (
    .load(or_1_out), .D(multiplexer_1_out), .count(not_2_out), .Q(counter_1_q), .clk(in_2), .clr(in_1));  // open: carry
  not not_2 (not_2_out, or_1_out);
  not not_3 (not_3_out, in_1);
  // REG8m_INC_LD reg8m_inc_ld_1: pin names not known; wires that end beside it: in_2, not_3_out, A7__0, BR7__0, ldBR
  ROM #(.addrWidth(7), .dataWidth(32)) rom_1 (
    .addr(counter_1_q),
    .data({rom_1_data, dc4_16_1_p1, clEXEC, stINTR, clPSWSTART, ldIVTP, mx0, mxRO0, shrB, mxPC1, ldSTART, ldI, ldDWL, ldDWH, incSP, decSP, ldMAR, mxMAR2, ldPC, mxPC0, mxA1, incB, rdMEM_t}));  // open: sel
  ROM #(.addrWidth(7), .dataWidth(21)) rom_2 (
    .addr(counter_1_q),
    .data({clB, \or , wrGPR, incMAR, mxMDR2, wrMEM_t, ldMDR, mxMDR1, mxMDR0, decMAR, decB, ldC, ldV, add, mxA0, mxB1, mxB0, ldB, clEXEC, stINTR, ldA}));  // open: sel
  // ALU8_ADD_SUB alu8_add_sub_1: pin names not known; wires that end beside it: Cout, A7__0, SUB7__0, B7__0, 1'b0, 1'b0, INSTRUCBUS[17]
  // KMOPR kmopr_1: pin names not known; wires that end beside it: kmopr_1_p1, INSTRUCBUS[14], INSTRUCBUS[15], INSTRUCBUS[0], INSTRUCBUS[3], INSTRUCBUS[4], INSTRUCBUS[5], INSTRUCBUS[6], INSTRUCBUS[7], INSTRUCBUS[8], INSTRUCBUS[9], INSTRUCBUS[10], INSTRUCBUS[11], INSTRUCBUS[12], INSTRUCBUS[13], INSTRUCBUS[1], INSTRUCBUS[2], INSTRUCBUS[16], INSTRUCBUS[17], INSTRUCBUS[20], INSTRUCBUS[21], INSTRUCBUS[22], INSTRUCBUS[19], INSTRUCBUS[18]
  and and_1 (and_1_out, brPOPPSW, POPPSW);
  not not_4 (not_4_out, PHASEFFBUS[2]);
  and and_2 (and_2_out, brnotStopLoop, ~stopLoop);  // AND_Gate
  not not_5 (not_5_out, in_3);
  and and_3 (and_3_out, not_4_out, brnotEXEC);
  and and_4 (and_4_out, regdir, brregdir);
  and and_5 (and_5_out, brorjmp, brbrorjmp);
  and and_6 (and_6_out, not_5_out, brnotFCBUS);
  or or_2 (brcnd, and_1_out, and_3_out, and_2_out, and_4_out, and_5_out, and_6_out);
  or or_3 (stopLoop, equal, MDRis0);

  // Other names for the same wires on the sheet: A15__0[15:0] = A; ALU7__0[7:0] = ALU; B15__0[15:0] = B; CLK = in_2;
  //   FCBUS = in_3; HALT = INSTRUCBUS[0]; RTS = INSTRUCBUS[1]; RTI = INSTRUCBUS[2]; INTE = INSTRUCBUS[3];
  //   INTD = INSTRUCBUS[4]; PUSH = INSTRUCBUS[5]; POP = INSTRUCBUS[6]; STBR = INSTRUCBUS[7]; STXR = INSTRUCBUS[8];
  //   STAR = INSTRUCBUS[9]; BNEQ = INSTRUCBUS[10]; BOVF = INSTRUCBUS[11]; JNNG = INSTRUCBUS[12];
  //   JGRT = INSTRUCBUS[13]; LD = INSTRUCBUS[14]; ST = INSTRUCBUS[15]; INC = INSTRUCBUS[16]; SUB = INSTRUCBUS[17];
  //   TST = INSTRUCBUS[18]; STRCPY = INSTRUCBUS[19]; JADR = INSTRUCBUS[20]; JMP = INSTRUCBUS[21];
  //   JSR = INSTRUCBUS[22]; EXEC = PHASEFFBUS[2]; INTR = PHASEFFBUS[3]; rst = in_1

  // Notes on the sheet:
  //   Operaciona jedinica
  //   Upravljacka jedinica
  //   Akumulator
  //   BR
  //   contents of rom_1 (hex, n*v repeats v):
  //   400000 600000 0 82200000 10200000 0 82200000 0 1c800000 0 14a00000 0 18a00000 82200000 82200000 0
  //   82200000 0 24a00001 24c00002 4 82200000 82e00000 82200018 82e00000 82200010 e0 36a00000 e0 3aa00000
  //   82200010 100 160 42a00001 200 60 48a00001 400 4 100 160 52a00001 800 60 58a00001 83001000 100 160
  //   60a00001 260 64a00001 400 82202010 4000 82200000 c000 82200000 100e0 74a00000 e0 78a00000 82200000
  //   20000 82200000 40000 380000
  //   contents of rom_2 (hex, n*v repeats v):
  //   0 0 1 6 38 3c1 6 c00 0 7000 8000 34000 8000 0 40000 80041 6 100000 4000 20000 41 6 4*0 16000 8000
  //   15000 8000 0 0 0 4000 0 0 4000 0 1 0 0 4000 0 0 4000 306 0 0 4000 0 4000 0 0 200 1 200 1 17000 8000
  //   17000 8000
endmodule

module INTR (
  input  in_1,
  input  in_2,
  input  in_3,
  input  [3:0] PHASEFFBUS,
  input  [10:0] INSTRUCBUS,
  input  [7:0] PSW,
  input  [3:0] intr,
  output [15:0] ADDIVTP,
  output [1:0] UEXT1__0,
  output inta,
  output [14:0] CMEMBUS,
  output [7:0] CFFBUS,
  output [8:0] CREGBUS,
  output rdMEM,
  output wrMEM
);


  // Other names for the same wires on the sheet: ADDIVTP15__0[15:0] = ADDIVTP; CLK = in_2; FCBUS = in_3;
  //   intr3__0[3:0] = intr; ldBR = inta; rst = in_1

  // Notes on the sheet:
  //   Operaciona jedinica
  //   Upravljacka jedinica
endmodule

module RAM (
  input  [15:0] in_1,
  input  in_2,
  input  [7:0] in_3,
  input  in_4,
  input  in_5,
  input  in_6,
  output [7:0] out_7,
  output out_8
);

  wire and_1_out, and_2_out, CNT0, LDCNT, not_1_out, notCNT0, or_1_out, reg4_ld_sl_sr_1_p6, rsff_2_p4,
       rsff_2_p5, rsff_3_p4, sl;
  wire [3:0] CNT, LFSR;

  // RSFF rsff_1: pin names not known; wires that end beside it: 1'b0, in_2, in_6, sl
  or or_1 (or_1_out, in_4, in_5);
  // REG4_LD_SL_SR reg4_ld_sl_sr_1: pin names not known; wires that end beside it: 1'b0, 1'b0, in_2, 4'b1111, LFSR, reg4_ld_sl_sr_1_p6, sl, in_6
  // RisingEdge risingedge_1: pin names not known; wires that end beside it: or_1_out, in_2, LDCNT
  // MEM64Kx8 mem64kx8_1: pin names not known; wires that end beside it: in_1, 1'b1, in_2, in_3, out_7, in_4
  xor xor_1 (reg4_ld_sl_sr_1_p6, LFSR[2], LFSR[3]);
  and and_1 (and_1_out, CNT0, not_1_out);
  not not_1 (not_1_out, LDCNT);
  // RSFF rsff_2: pin names not known; wires that end beside it: and_1_out, in_2, LDCNT, rsff_2_p4, rsff_2_p5
  not not_2 (rsff_2_p4, in_6);
  and and_2 (and_2_out, rsff_2_p5, CNT0);
  // REG4m_DEC_LD reg4m_dec_ld_1: pin names not known; wires that end beside it: in_2, LFSR, CNT, LDCNT, notCNT0, notCNT0
  or or_2 (notCNT0, CNT[0], CNT[1], CNT[2], CNT[3]);
  // RSFF rsff_3: pin names not known; wires that end beside it: out_8, in_2, and_2_out, rsff_3_p4, out_8
  not not_3 (rsff_3_p4, in_6);
  not not_4 (CNT0, notCNT0);

  // Other names for the same wires on the sheet: ADR[15:0] = in_1; CLK = in_2; DIN[7:0] = in_3; DOUT[7:0] = out_7;
  //   fc = out_8; RDMEM = in_5; rst = in_6; WRMEM = in_4

  // Notes on the sheet:
  //   Random broj predstavlja vreme pristupa memoriji
  //   Brojac za generisanje random broja 
  //   Jedinica za generisanje function complete (fc) signala
  //   Brojac za dekrementiranje random broja
endmodule
