// Logisim project main3.circ as structural Verilog: 8 circuits, main circuit COMPUTER
module COMPUTER (
);

  wire BTN_RST_out, CLK, cpu_1_inta, interrupt_interface_4_1_p1, interrupt_interface_4_1_p2,
       interrupt_interface_4_1_p3, interrupt_interface_4_1_p4, interrupt_interface_8_1_p4,
       interrupt_interface_8_1_p5, interrupt_interface_8_1_p6, interrupt_interface_8_1_p7,
       interrupt_interface_8_1_p8, interrupt_interface_8_1_p9, interrupt_interface_8_1_p10,
       interrupt_interface_8_1_p11, pull_resistor_3_node, pull_resistor_6_node, ram_1_out_8, rst;
  wire [2:0] cpu_1_uext1__0;
  wire [7:0] interrupt_interface_8_1_p1, pull_resistor_2_node, ram_1_out_7;
  wire [15:0] pull_resistor_4_node;

  Button BTN_RST (.out(BTN_RST_out));
  Clock u_CLK (.out(CLK));
  // RisingEdge risingedge_1: pin names not known; wires that end beside it: BTN_RST_out, CLK, rst
  RAM ram_1 (
    .in_1(pull_resistor_4_node), .in_2(CLK), .in_3(pull_resistor_2_node), .in_4(pull_resistor_3_node),
    .in_5(pull_resistor_6_node), .in_6(rst), .out_7(ram_1_out_7), .out_8(ram_1_out_8));
  Pull_Resistor pull_resistor_1 (.node(ram_1_out_7));
  Pull_Resistor pull_resistor_2 (.node(pull_resistor_2_node));
  Pull_Resistor pull_resistor_3 (.node(pull_resistor_3_node));
  Pull_Resistor pull_resistor_4 (.node(pull_resistor_4_node));
  Pull_Resistor pull_resistor_5 (.node(ram_1_out_8));
  Pull_Resistor pull_resistor_6 (.node(pull_resistor_6_node));
  CPU cpu_1 (
    .in_1(rst), .in_2(CLK), .in_3(ram_1_out_8), .in_4(ram_1_out_7), .ABUS(pull_resistor_4_node),
    .DOUTBUS(pull_resistor_2_node), .out_8(pull_resistor_3_node), .out_9(pull_resistor_6_node),
    .inta(cpu_1_inta), .intr3__0(interrupt_interface_8_1_p1), .UEXT1__0(cpu_1_uext1__0));
  // INTERRUPT_INTERFACE_8 interrupt_interface_8_1: pin names not known; wires that end beside it: interrupt_interface_8_1_p1, cpu_1_inta, cpu_1_uext1__0, interrupt_interface_8_1_p4, interrupt_interface_8_1_p5, interrupt_interface_8_1_p6, interrupt_interface_8_1_p7, interrupt_interface_8_1_p8, interrupt_interface_8_1_p9, interrupt_interface_8_1_p10, interrupt_interface_8_1_p11, CLK
  Button BTN_INTR7 (.out(interrupt_interface_8_1_p4));
  Button BTN_INTR6 (.out(interrupt_interface_8_1_p5));
  Button BTN_INTR5 (.out(interrupt_interface_8_1_p6));
  Button BTN_INTR4 (.out(interrupt_interface_8_1_p7));
  Button BTN_INTR3 (.out(interrupt_interface_8_1_p8));
  Button BTN_INTR2 (.out(interrupt_interface_8_1_p9));
  Button BTN_INTR1 (.out(interrupt_interface_8_1_p10));
  Button BTN_INTR0 (.out(interrupt_interface_8_1_p11));
  // INTERRUPT_INTERFACE_4 interrupt_interface_4_1: pin names not known; wires that end beside it: interrupt_interface_4_1_p1, interrupt_interface_4_1_p2, interrupt_interface_4_1_p3, interrupt_interface_4_1_p4, CLK
  Button BTN_INTR3_2 (.out(interrupt_interface_4_1_p1));
  Button BTN_INTR2_2 (.out(interrupt_interface_4_1_p2));
  Button BTN_INTR1_2 (.out(interrupt_interface_4_1_p3));
  Button BTN_INTR0_2 (.out(interrupt_interface_4_1_p4));
endmodule

module CPU (
  input  in_1,
  input  in_2,
  input  in_3,
  input  [7:0] in_4,
  input  [7:0] intr3__0,
  output [15:0] ABUS,
  output [7:0] DOUTBUS,
  output out_8,
  output out_9,
  output inta,
  output [2:0] UEXT1__0
);

  wire [3:0] common_1_phaseffbus;
  wire [5:0] common_1_addrbus, pull_resistor_2_node;
  wire [7:0] ALU;
  wire [9:0] pull_resistor_5_node;
  wire [14:0] pull_resistor_6_node;
  wire [15:0] A, B, INTRADDR, PSW, undriven;
  wire [19:0] pull_resistor_7_node;
  wire [31:0] common_1_instrucbus;

  COMMON common_1 (
    .CLK(in_2), .RST(in_1), .DIN(in_4), .CMEMBUS(pull_resistor_6_node), .MAR(ABUS), .MDR(DOUTBUS),
    .PHASEFFBUS(common_1_phaseffbus), .INSTRUCBUS(common_1_instrucbus), .ADDRBUS(common_1_addrbus),
    .PSW(PSW), .CREGBUS(pull_resistor_7_node), .CFFBUS(pull_resistor_5_node), .B(B), .A(A),
    .CPSW(pull_resistor_2_node), .ALU(ALU), .IVTPPDSP(INTRADDR));
  Pull_Resistor pull_resistor_1 (.node(common_1_phaseffbus));
  Pull_Resistor pull_resistor_2 (.node(pull_resistor_2_node));
  Pull_Resistor pull_resistor_3 (.node(common_1_instrucbus));
  Pull_Resistor pull_resistor_4 (.node(common_1_addrbus));
  Pull_Resistor pull_resistor_5 (.node(pull_resistor_5_node));
  Pull_Resistor pull_resistor_6 (.node(pull_resistor_6_node));
  Pull_Resistor pull_resistor_7 (.node(pull_resistor_7_node));
  FETCH fetch_1 (
    .in_1(in_1), .in_2(in_2), .in_3(in_3), .PHASEFFBUS(common_1_phaseffbus),
    .INSTRUCBUS(common_1_instrucbus), .ADDRBUS(common_1_addrbus), .PSW(PSW), .rdMEM(out_9),
    .CMEMBUS(pull_resistor_6_node), .CFFBUS(pull_resistor_5_node), .CREGBUS(pull_resistor_7_node));
  ADDR addr_1 (
    .in_1(in_1), .in_2(in_2), .in_3(in_3), .PHASEFFBUS(common_1_phaseffbus),
    .INSTRUCBUS(common_1_instrucbus), .ADDRBUS(common_1_addrbus), .rdMEM(out_9),
    .CMEMBUS(pull_resistor_6_node), .CFFBUS(pull_resistor_5_node), .CREGBUS(pull_resistor_7_node));
  EXEC exec_1 (
    .in_1(in_1), .in_2(in_2), .in_3(in_3), .B(B), .PHASEFFBUS(common_1_phaseffbus),
    .INSTRUCBUS(common_1_instrucbus), .ADDRBUS(common_1_addrbus), .PSW(PSW), .A(A), .ALU(ALU),
    .CMEMBUS(pull_resistor_6_node), .CFFBUS(pull_resistor_5_node), .CREGBUS(pull_resistor_7_node),
    .CPSW(pull_resistor_2_node), .rdMEM(out_9), .wrMEM(out_8));
  INTR intr_1 (
    .in_1(in_1), .in_2(in_2), .in_3(in_3), .PHASEFFBUS(common_1_phaseffbus),
    .INSTRUCBUS(common_1_instrucbus), .PSW(PSW), .intr(intr3__0), .ADDIVTP(INTRADDR),
    .CMEMBUS(pull_resistor_6_node), .CFFBUS(pull_resistor_5_node), .CREGBUS(pull_resistor_7_node),
    .rdMEM(out_9), .wrMEM(out_8), .UEXT1__0(UEXT1__0), .inta(inta), .ACC(undriven));

  // Other names for the same wires on the sheet: CLK = in_2; DIN7__0[7:0] = in_4; FCBUS = in_3;
  //   intr7__0[7:0] = intr3__0; MAR[15:0] = ABUS; MDR[7:0] = DOUTBUS; RD = out_9; rst = in_1; WR = out_8
endmodule

module COMMON (
  input  CLK,
  input  RST,
  input  [7:0] DIN,
  input  [15:0] A,
  input  [7:0] ALU,
  input  [15:0] IVTPPDSP,
  input  [14:0] CMEMBUS,
  input  [9:0] CFFBUS,
  input  [19:0] CREGBUS,
  input  [5:0] CPSW,
  output [15:0] MAR,
  output [7:0] MDR,
  output [3:0] PHASEFFBUS,
  output [31:0] INSTRUCBUS,
  output [5:0] ADDRBUS,
  output [15:0] PSW,
  output [15:0] B
);

  wire ADR, adrinst, and_1_out, and_2_out, and_3_out, and_4_out, and_5_out, and_6_out, and_7_out, and_8_out,
       and_9_out, and_10_out, bezadrinst, branchinst, clB, dc4_16_1_p3, dc4_16_1_p4, dc4_16_1_p5,
       dc4_16_5_p1, decB, incB, jmpinst, mp2_16b_1_p3, mp4_16b_1_p5, mp4_16b_2_p5, mp8_8b_1_p7, mp8_8b_1_p13,
       mp8_16b_1_p7, mp8_16b_1_p9, not_1_out, not_5_out, reg16_inc_ld_2_p4, rsff_2_p4, rsff_3_p10, rsff_4_p4,
       rsff_6_p4, rsff_7_p4, rsff_8_p3, rsff_8_p4, shrB;
  wire [3:0] IR27__24;
  wire [7:0] DWH7__0, DWL7__0, IR7__0, IR15__8, IR23__16;
  wire [7:4] IR31__24;
  wire [15:0] ADDPCREL15__0, AR15__0, BR15__0, DR15__0, PC15__0, SP15__0;

  // REG8_LD reg8_ld_1: pin names not known; wires that end beside it: CLK, MDR, IR23__16, CREGBUS[2]
  // Probe on IR23__16
  // MP8_16b mp8_16b_1: pin names not known; wires that end beside it: CREGBUS[5], CMEMBUS[6], CMEMBUS[7], PC15__0, {IR15__8, IR7__0}, SP15__0, mp8_16b_1_p7, AR15__0, mp8_16b_1_p9, mp8_16b_1_p9, 1'b1
  // REG16_INC_LD reg16_inc_ld_1: pin names not known; wires that end beside it: CLK, mp8_16b_1_p7, MAR, CMEMBUS[0], CMEMBUS[1]
  // Probe on MAR
  // REG8_LD reg8_ld_2: pin names not known; wires that end beside it: CLK, MDR, {IR31__24, IR27__24}, CREGBUS[3]
  // DC4_16 dc4_16_1: pin names not known; wires that end beside it: IR31__24, PSW[0], dc4_16_1_p3, dc4_16_1_p4, dc4_16_1_p5, adrinst, jmpinst, bezadrinst, branchinst, dc4_16_1_p3, dc4_16_1_p4, dc4_16_1_p5
  // DC4_16 dc4_16_2: pin names not known; wires that end beside it: IR27__24, adrinst, INSTRUCBUS[14], INSTRUCBUS[15], INSTRUCBUS[16], INSTRUCBUS[17], INSTRUCBUS[18], INSTRUCBUS[19], INSTRUCBUS[20]
  // MP4_16b mp4_16b_1: pin names not known; wires that end beside it: CREGBUS[6], CREGBUS[5], {{8{1'b0}}, MDR}, {IR15__8, IR7__0}, mp4_16b_1_p5, mp4_16b_1_p5, {DWH7__0, DWL7__0}, DR15__0, 1'b1
  // REG16 reg16_1: pin names not known; wires that end beside it: clB, shrB, CLK, B, CREGBUS[4], incB, decB
  // Probe on {IR31__24, IR27__24}
  // Probe on B
  // REG8_LD reg8_ld_3: pin names not known; wires that end beside it: CLK, MDR, IR15__8, CREGBUS[1]
  // Probe on IR15__8
  // ADD16 add16_1: pin names not known; wires that end beside it: {{9{IR23__16[7]}}, IR23__16[6:0]}, ADDPCREL15__0, PC15__0
  // MP8_8b mp8_8b_1: pin names not known; wires that end beside it: CMEMBUS[8], CMEMBUS[9], CMEMBUS[10], DIN, A[15:8], A[7:0], mp8_8b_1_p7, PC15__0[15:8], PC15__0[7:0], PSW[15:8], PSW[7:0], 1'b1, mp8_8b_1_p13, mp8_8b_1_p13
  // Probe on mp8_8b_1_p7
  // REG8_LD reg8_ld_4: pin names not known; wires that end beside it: CLK, mp8_8b_1_p7, MDR, CMEMBUS[2]
  // Probe on MDR
  // DC4_16 dc4_16_3: pin names not known; wires that end beside it: IR27__24, bezadrinst, INSTRUCBUS[0], INSTRUCBUS[1], INSTRUCBUS[2], INSTRUCBUS[3], INSTRUCBUS[4], INSTRUCBUS[5], INSTRUCBUS[6], INSTRUCBUS[7], INSTRUCBUS[8], INSTRUCBUS[9]
  // DC4_16 dc4_16_4: pin names not known; wires that end beside it: IR27__24, jmpinst, INSTRUCBUS[21], INSTRUCBUS[22]
  // REG8_LD reg8_ld_5: pin names not known; wires that end beside it: CLK, MDR, IR7__0, CREGBUS[0]
  // Probe on IR7__0
  // REG8_LD reg8_ld_6: pin names not known; wires that end beside it: CLK, MDR, DWH7__0, CREGBUS[14]
  // OR_Gate or_1 is placed but not wired
  // MP4_16b mp4_16b_2: pin names not known; wires that end beside it: CMEMBUS[11], CMEMBUS[12], {IR15__8, IR7__0}, {DWH7__0, DWL7__0}, mp4_16b_2_p5, B, 1'b1, MAR
  // DC2_4 dc2_4_1: pin names not known; wires that end beside it: IR27__24[3:2], branchinst, INSTRUCBUS[10], INSTRUCBUS[11], INSTRUCBUS[12], INSTRUCBUS[13]
  // DC4_16 dc4_16_5: pin names not known; wires that end beside it: dc4_16_5_p1, dc4_16_5_p1, IR23__16[7:4], adrinst, ADDRBUS[0], ADDRBUS[1], ADDRBUS[2], ADDRBUS[3], ADDRBUS[4], ADDRBUS[5]
  // REG16 reg16_2: pin names not known; wires that end beside it: CLK, 16'hf000, SP15__0, RST, CREGBUS[12], CMEMBUS[13]
  not not_1 (not_1_out, RST);
  // RSFF rsff_1: pin names not known; wires that end beside it: CFFBUS[1], CLK, CFFBUS[0], not_1_out, PHASEFFBUS[0]
  // MP2_16b mp2_16b_1: pin names not known; wires that end beside it: RST, mp4_16b_2_p5, mp2_16b_1_p3, 16'h1000, 1'b1
  // Probe on mp2_16b_1_p3
  // REG16_INC_LD reg16_inc_ld_2: pin names not known; wires that end beside it: CLK, mp2_16b_1_p3, PC15__0, reg16_inc_ld_2_p4, CMEMBUS[4]
  // Probe on PC15__0
  // REG8_LD reg8_ld_7: pin names not known; wires that end beside it: CLK, MDR, DWL7__0, CREGBUS[13]
  // Probe on SP15__0
  or or_2 (reg16_inc_ld_2_p4, CMEMBUS[3], RST);
  // RSFF rsff_2: pin names not known; wires that end beside it: CFFBUS[3], CLK, CFFBUS[2], rsff_2_p4, PHASEFFBUS[1]
  not not_2 (rsff_2_p4, RST);
  // Probe on B
  // REG16_INC_LD reg16_inc_ld_3: pin names not known; wires that end beside it: CLK, A, DR15__0, CREGBUS[8]
  and and_1 (and_1_out, A[0], A[1], A[2], A[3], A[4], A[5], A[6], A[7], A[9], A[10], A[11], A[12], A[13], A[14], A[15], A[8]);
  // Probe on DR15__0
  // RSFF rsff_3: pin names not known; wires that end beside it: B[0], B[1], B[2], B[3], B[4], B[5], CFFBUS[5], CLK, CFFBUS[4], rsff_3_p10, PHASEFFBUS[2]
  not not_3 (rsff_3_p10, RST);
  or or_3 (ADR, INSTRUCBUS[14], INSTRUCBUS[17], INSTRUCBUS[16]);
  and and_2 (and_2_out, ADR, and_3_out);
  and and_3 (and_3_out, ~A[0], ~A[1], ~A[2], ~A[3], ~A[4], ~A[5], ~A[6], ~A[7], ~A[8], ~A[9], ~A[10], ~A[11], ~A[12], ~A[13], ~A[14], ~A[15]);  // AND_Gate
  and and_4 (and_4_out, A[15], ADR);
  and and_5 (and_5_out, INSTRUCBUS[16], and_1_out);
  // REG16_INC_LD reg16_inc_ld_4: pin names not known; wires that end beside it: CLK, A, AR15__0, CREGBUS[8]
  // Probe on AR15__0
  and and_6 (and_6_out, ~and_2_out, CREGBUS[18]);  // AND_Gate
  and and_7 (and_7_out, and_2_out, CREGBUS[18]);
  and and_8 (and_8_out, ~and_4_out, CREGBUS[17]);  // AND_Gate
  and and_9 (and_9_out, and_4_out, CREGBUS[17]);
  // RSFF rsff_4: pin names not known; wires that end beside it: CFFBUS[7], CLK, CFFBUS[6], rsff_4_p4, PHASEFFBUS[3]
  not not_4 (rsff_4_p4, RST);
  not not_5 (not_5_out, RST);
  // RSFF rsff_5: pin names not known; wires that end beside it: CFFBUS[8], CLK, not_5_out, PSW[0]
  // RSFF rsff_6: pin names not known; wires that end beside it: and_6_out, CLK, and_7_out, rsff_6_p4, PSW[3]
  not not_6 (rsff_6_p4, RST);
  // RSFF rsff_7: pin names not known; wires that end beside it: and_8_out, CLK, and_9_out, rsff_7_p4, PSW[4]
  not not_7 (rsff_7_p4, RST);
  and and_10 (and_10_out, ~and_5_out, CREGBUS[19]);  // AND_Gate
  // RSFF rsff_8: pin names not known; wires that end beside it: and_10_out, CLK, rsff_8_p3, rsff_8_p4, PSW[1]
  and and_11 (rsff_8_p3, and_5_out, CREGBUS[19]);
  not not_8 (rsff_8_p4, RST);
  // REG16_INC_LD reg16_inc_ld_5: pin names not known; wires that end beside it: CLK, A, BR15__0, CREGBUS[8]
  // Probe on BR15__0

  assign CPSW[0] = CFFBUS[8];
  assign CREGBUS[11] = CMEMBUS[13];

  // Other names for the same wires on the sheet: MDR7__0[7:0] = MDR; A7__0[7:0] = A[7:0]; A15__0[15:0] = A;
  //   A15__8[7:0] = A[15:8]; immed = ADDRBUS[0]; memdir = ADDRBUS[1]; regdir = ADDRBUS[2]; regind = ADDRBUS[3];
  //   brpom = ADDRBUS[4]; bxpom = ADDRBUS[5]; ALU7__0[7:0] = ALU; B7__0[7:0] = B[7:0]; B15__0[15:0] = B;
  //   stariji[7:0] = B[15:8]; stFETCH = CFFBUS[0]; clFETCH = CFFBUS[1]; stADDR = CFFBUS[2]; clADDR = CFFBUS[3];
  //   stEXEC = CFFBUS[4]; clEXEC = CFFBUS[5]; stINTR = CFFBUS[6]; clINTR = CFFBUS[7]; ldMAR = CMEMBUS[0];
  //   incMAR = CMEMBUS[1]; ldMDR = CMEMBUS[2]; ldPC = CMEMBUS[3]; incPC = CMEMBUS[4]; mxMAR2 = CMEMBUS[5];
  //   mxMAR1 = CMEMBUS[6]; mxMAR0 = CMEMBUS[7]; mxMDR2 = CMEMBUS[8]; mxMDR1 = CMEMBUS[9]; mxMDR0 = CMEMBUS[10];
  //   mxPC1 = CMEMBUS[11]; mxPC0 = CMEMBUS[12]; clPSWSTART = CFFBUS[8]; ldIR7__0 = CREGBUS[0]; ldIR15__8 = CREGBUS[1];
  //   ldIR23__16 = CREGBUS[2]; ldIR31__24 = CREGBUS[3]; ldB = CREGBUS[4]; mxB0 = CREGBUS[5]; mxB1 = CREGBUS[6];
  //   ldA = CREGBUS[7]; ldDR = CREGBUS[8]; incA = CREGBUS[9]; mxA0 = CREGBUS[10]; decSP = CMEMBUS[13];
  //   incSP = CREGBUS[12]; ldDWL = CREGBUS[13]; ldDWH = CREGBUS[14]; ldSTAR = CREGBUS[15]; ldSTBR = CREGBUS[16];
  //   ldN = CREGBUS[17]; ldZ = CREGBUS[18]; ldV = CREGBUS[19]; Din7__0[7:0] = DIN; ENTRADDR15__0[15:0] = IVTPPDSP;
  //   HALT = INSTRUCBUS[0]; RTS = INSTRUCBUS[1]; RTI = INSTRUCBUS[2]; INTE = INSTRUCBUS[3]; INTD = INSTRUCBUS[4];
  //   PUSH = INSTRUCBUS[5]; POP = INSTRUCBUS[6]; STBR = INSTRUCBUS[7]; STXR = INSTRUCBUS[8]; STAR = INSTRUCBUS[9];
  //   BNEQ = INSTRUCBUS[10]; BOVF = INSTRUCBUS[11]; JNNG = INSTRUCBUS[12]; JGRT = INSTRUCBUS[13]; LD = INSTRUCBUS[14];
  //   ST = INSTRUCBUS[15]; INC = INSTRUCBUS[16]; SUB = INSTRUCBUS[17]; TST = INSTRUCBUS[18]; STRCPY = INSTRUCBUS[19];
  //   JADR = INSTRUCBUS[20]; JMP = INSTRUCBUS[21]; JSR = INSTRUCBUS[22]; IR31__24[3:0] = IR27__24;
  //   MAR15__0[15:0] = MAR; FETCH = PHASEFFBUS[0]; ADDR = PHASEFFBUS[1]; EXEC = PHASEFFBUS[2]; INTR = PHASEFFBUS[3];
  //   PSW15__0[15:0] = PSW; PSWSTART = PSW[0]; PSWV = PSW[1]; PSWC = PSW[2]; PSWZ = PSW[3]; PSWN = PSW[4]

  // Notes on the sheet:
  //   Sabirac
  //   Sabirac
  //   Instrukcijski registar
  //   Pomocni registri
  //   MAR
  //   Dekoderi za prepoznavanje instrukcije na osnovu sadrzaja registra IR23..16
  //   MDR
  //   SP
  //   PC
  //   Dekoderi za prepoznavanje nacina adresiranja
  //   DW
  //   FF za pokretanje FETCH, ADDR, EXEC i INTR faze izvršavanja instrukcije
  //   Registarski fajl
  //   DR
  //   Programska statusna reč (PSW)
  //   AR
  //   BR
endmodule

module FETCH (
  input  in_1,
  input  in_2,
  input  in_3,
  input  [3:0] PHASEFFBUS,
  input  [31:0] INSTRUCBUS,
  input  [5:0] ADDRBUS,
  input  [15:0] PSW,
  output [14:0] CMEMBUS,
  output [9:0] CFFBUS,
  output [19:0] CREGBUS,
  output rdMEM
);

  wire addr2, addr3, addr4, addr_t, and_4_out, and_5_out, and_6_out, and_7_out, and_8_out, and_9_out,
       and_10_out, and_11_out, bezadr1, bradr1, bradr2, bradr3, bradr4, brbezadr1, brcnd, brjmp2, brjmp3,
       brnotfcmem, bruncnd, clFETCH, incPC, jmp2, jmp3, ldIR7__0, ldIR15__8, ldIR23__16, ldIR31__24, ldMAR,
       ldMDR, not_1_out, not_3_out, not_4_out, not_5_out, notPSWSTandFETCH, or_4_out, or_6_out, or_7_out,
       or_8_out, rdMEM_t, reg5_cl_inc_ld_1_p5, reg5_cl_inc_ld_1_p6, stADDR, stEXEC;
  wire [4:0] reg5_cl_inc_ld_1_p4;
  wire [19:11] reg5_cl_inc_ld_1_p3;

  not not_1 (not_1_out, in_1);
  // REG5_CL_INC_LD reg5_cl_inc_ld_1: pin names not known; wires that end beside it: in_2, not_1_out, reg5_cl_inc_ld_1_p3[19:15], reg5_cl_inc_ld_1_p4, reg5_cl_inc_ld_1_p5, reg5_cl_inc_ld_1_p6
  or or_1 (jmp2, INSTRUCBUS[10], INSTRUCBUS[11]);
  or or_2 (jmp3, INSTRUCBUS[12], INSTRUCBUS[21], INSTRUCBUS[22], INSTRUCBUS[13]);
  or or_3 (reg5_cl_inc_ld_1_p5, bruncnd, brcnd);
  not not_2 (reg5_cl_inc_ld_1_p6, reg5_cl_inc_ld_1_p5);
  or or_4 (or_4_out, ADDRBUS[2], ADDRBUS[3]);
  ROM #(.addrWidth(5), .dataWidth(20)) rom_1 (
    .addr(reg5_cl_inc_ld_1_p4),
    .data({reg5_cl_inc_ld_1_p3, stEXEC, stADDR, clFETCH, ldIR7__0, ldIR15__8, ldIR23__16, ldIR31__24, ldMDR, rdMEM_t, incPC, ldMAR}),
    .sel(1'b1));
  and and_1 (addr2, addr_t, or_4_out);
  or or_5 (addr_t, INSTRUCBUS[14], INSTRUCBUS[15], INSTRUCBUS[16], INSTRUCBUS[17], INSTRUCBUS[18], INSTRUCBUS[19], INSTRUCBUS[20]);
  // DC4_16 dc4_16_1: pin names not known; wires that end beside it: reg5_cl_inc_ld_1_p3[14:11], 1'b1, brjmp2, bruncnd, notPSWSTandFETCH, brbezadr1, bradr1, bradr2, bradr3, brjmp3, bradr4, brnotfcmem
  or or_6 (or_6_out, ADDRBUS[0], ADDRBUS[1]);
  or or_7 (or_7_out, ADDRBUS[4], ADDRBUS[5]);
  and and_2 (addr4, addr_t, or_6_out);
  and and_3 (addr3, addr_t, or_7_out);
  not not_3 (not_3_out, PHASEFFBUS[0]);
  not not_4 (not_4_out, PSW[0]);
  or or_8 (or_8_out, not_3_out, not_4_out);
  not not_5 (not_5_out, in_3);
  or or_9 (bezadr1, INSTRUCBUS[0], INSTRUCBUS[1], INSTRUCBUS[2], INSTRUCBUS[3], INSTRUCBUS[4], INSTRUCBUS[5], INSTRUCBUS[6], INSTRUCBUS[7], INSTRUCBUS[8], INSTRUCBUS[9]);
  and and_4 (and_4_out, or_8_out, notPSWSTandFETCH);
  and and_5 (and_5_out, brbezadr1, bezadr1);
  and and_6 (and_6_out, brjmp2, jmp2);
  and and_7 (and_7_out, bradr2, addr2);
  and and_8 (and_8_out, brjmp3, jmp3);
  and and_9 (and_9_out, brnotfcmem, not_5_out);
  and and_10 (and_10_out, bradr3, addr3);
  and and_11 (and_11_out, bradr4, addr4);
  or or_10 (brcnd, and_4_out, and_5_out, and_6_out, and_7_out, and_8_out, and_9_out, and_10_out, and_11_out);
  assign CMEMBUS[0] = ldMAR ? 1'b1 : 1'bz;  // Controlled_Buffer controlled_buffer_1
  assign CMEMBUS[2] = ldMDR ? 1'b1 : 1'bz;  // Controlled_Buffer controlled_buffer_2
  assign CMEMBUS[4] = incPC ? 1'b1 : 1'bz;  // Controlled_Buffer controlled_buffer_3
  assign CFFBUS[1] = clFETCH ? 1'b1 : 1'bz;  // Controlled_Buffer controlled_buffer_4
  assign CFFBUS[2] = stADDR ? 1'b1 : 1'bz;  // Controlled_Buffer controlled_buffer_5
  assign CFFBUS[4] = stEXEC ? 1'b1 : 1'bz;  // Controlled_Buffer controlled_buffer_6
  assign CREGBUS[0] = ldIR7__0 ? 1'b1 : 1'bz;  // Controlled_Buffer controlled_buffer_7
  assign CREGBUS[1] = ldIR15__8 ? 1'b1 : 1'bz;  // Controlled_Buffer controlled_buffer_8
  assign CREGBUS[2] = ldIR23__16 ? 1'b1 : 1'bz;  // Controlled_Buffer controlled_buffer_9
  assign CREGBUS[3] = ldIR31__24 ? 1'b1 : 1'bz;  // Controlled_Buffer controlled_buffer_10
  assign rdMEM = rdMEM_t ? 1'b1 : 1'bz;  // Controlled_Buffer controlled_buffer_11

  // Other names for the same wires on the sheet: immed = ADDRBUS[0]; memdir = ADDRBUS[1]; regdir = ADDRBUS[2];
  //   regind = ADDRBUS[3]; brpom = ADDRBUS[4]; bxpom = ADDRBUS[5]; CLK = in_2; FCBUS = in_3; HALT = INSTRUCBUS[0];
  //   RTS = INSTRUCBUS[1]; RTI = INSTRUCBUS[2]; INTE = INSTRUCBUS[3]; INTD = INSTRUCBUS[4]; PUSH = INSTRUCBUS[5];
  //   POP = INSTRUCBUS[6]; STBR = INSTRUCBUS[7]; STXR = INSTRUCBUS[8]; STAR = INSTRUCBUS[9]; BNEQ = INSTRUCBUS[10];
  //   BOVF = INSTRUCBUS[11]; JNNG = INSTRUCBUS[12]; JGRT = INSTRUCBUS[13]; LD = INSTRUCBUS[14]; ST = INSTRUCBUS[15];
  //   INC = INSTRUCBUS[16]; SUB = INSTRUCBUS[17]; TST = INSTRUCBUS[18]; STRCPY = INSTRUCBUS[19];
  //   JADR = INSTRUCBUS[20]; JMP = INSTRUCBUS[21]; JSR = INSTRUCBUS[22]; FETCH = PHASEFFBUS[0]; ADDR = PHASEFFBUS[1];
  //   EXEC = PHASEFFBUS[2]; INTR = PHASEFFBUS[3]; PSWSTART = PSW[0]; rst = in_1

  // Notes on the sheet:
  //   Operaciona jedinica
  //   Kontrolna jedinica
  //   contents of rom_1 (hex, n*v repeats v):
  //   1000 3 1500c 10 9a000 a1800 3 3d00c 20 a3000 9a800 3 6500c 40 a3800 9c000 3 8d00c 80 b00 d00
endmodule

module ADDR (
  input  in_1,
  input  in_2,
  input  in_3,
  input  [3:0] PHASEFFBUS,
  input  [31:0] INSTRUCBUS,
  input  [5:0] ADDRBUS,
  output [14:0] CMEMBUS,
  output [9:0] CFFBUS,
  output [19:0] CREGBUS,
  output rdMEM
);

  wire and_1_out, and_2_out, and_3_out, bradr, brcnd, brnotADDR, brnotFCBUS, brST_STRFIND, bruncnd, clADDR,
       ldB, ldMAR, ldMRD, mxB0, mxB1, mxMAR0, mxMAR1, not_1_out, not_3_out, not_4_out, rdMEM_t,
       reg5_cl_inc_ld_1_p6, reg5_cl_inc_ld_1_p7, stEXEC;
  wire [4:0] kmadr_1_p5, multiplexer_1_out, reg5_cl_inc_ld_1_p5, rom_1_data_2;
  wire [17:10] rom_1_data;

  // KMADR kmadr_1: pin names not known; wires that end beside it: ADDRBUS[0], ADDRBUS[1], ADDRBUS[2], ADDRBUS[3], kmadr_1_p5, ADDRBUS[4], 1'b0, 1'b0
  Multiplexer #(.width(5), .enable("false")) multiplexer_1 (
    .in0(rom_1_data[17:13]), .in1(kmadr_1_p5), .out(multiplexer_1_out), .sel(bradr));
  not not_1 (not_1_out, in_1);
  // REG5_CL_INC_LD reg5_cl_inc_ld_1: pin names not known; wires that end beside it: 1'b0, in_2, not_1_out, multiplexer_1_out, reg5_cl_inc_ld_1_p5, reg5_cl_inc_ld_1_p6, reg5_cl_inc_ld_1_p7
  not not_2 (reg5_cl_inc_ld_1_p7, reg5_cl_inc_ld_1_p6);
  or or_1 (reg5_cl_inc_ld_1_p6, bruncnd, brcnd, bradr);
  ROM #(.addrWidth(5), .dataWidth(23)) rom_1 (
    .addr(reg5_cl_inc_ld_1_p5),
    .data({rom_1_data_2, rom_1_data, stEXEC, clADDR, ldMRD, rdMEM_t, mxMAR1, mxB1, mxMAR0, ldMAR, mxB0, ldB}),
    .sel(1'b1));
  // DC3_8 dc3_8_1: pin names not known; wires that end beside it: rom_1_data[12:10], 1'b1, bruncnd, brnotADDR, brST_STRFIND, brnotFCBUS, bradr
  not not_3 (not_3_out, PHASEFFBUS[1]);
  not not_4 (not_4_out, in_3);
  and and_1 (and_1_out, not_3_out, brnotADDR);
  and and_2 (and_2_out, INSTRUCBUS[15], brST_STRFIND);
  and and_3 (and_3_out, brnotFCBUS, not_4_out);
  or or_2 (brcnd, and_1_out, and_2_out, and_3_out);
  assign CMEMBUS[0] = ldMAR ? 1'b1 : 1'bz;  // Controlled_Buffer controlled_buffer_1
  assign CMEMBUS[6] = mxMAR1 ? 1'b1 : 1'bz;  // Controlled_Buffer controlled_buffer_2
  assign CMEMBUS[7] = mxMAR0 ? 1'b1 : 1'bz;  // Controlled_Buffer controlled_buffer_3
  assign CFFBUS[3] = clADDR ? 1'b1 : 1'bz;  // Controlled_Buffer controlled_buffer_4
  assign CFFBUS[4] = stEXEC ? 1'b1 : 1'bz;  // Controlled_Buffer controlled_buffer_5
  assign CREGBUS[4] = ldB ? 1'b1 : 1'bz;  // Controlled_Buffer controlled_buffer_6
  assign CREGBUS[5] = mxB0 ? 1'b1 : 1'bz;  // Controlled_Buffer controlled_buffer_7
  assign CREGBUS[6] = mxB1 ? 1'b1 : 1'bz;  // Controlled_Buffer controlled_buffer_8
  assign rdMEM = rdMEM_t ? 1'b1 : 1'bz;  // Controlled_Buffer controlled_buffer_9

  // Other names for the same wires on the sheet: immed = ADDRBUS[0]; memdir = ADDRBUS[1]; regdir = ADDRBUS[2];
  //   regind = ADDRBUS[3]; brpom = ADDRBUS[4]; bxpom = ADDRBUS[5]; CLK = in_2; FCBUS = in_3; HALT = INSTRUCBUS[0];
  //   RTS = INSTRUCBUS[1]; RTI = INSTRUCBUS[2]; INTE = INSTRUCBUS[3]; INTD = INSTRUCBUS[4]; PUSH = INSTRUCBUS[5];
  //   POP = INSTRUCBUS[6]; STBR = INSTRUCBUS[7]; STXR = INSTRUCBUS[8]; STAR = INSTRUCBUS[9]; BNEQ = INSTRUCBUS[10];
  //   BOVF = INSTRUCBUS[11]; JNNG = INSTRUCBUS[12]; JGRT = INSTRUCBUS[13]; LD = INSTRUCBUS[14]; ST = INSTRUCBUS[15];
  //   INC = INSTRUCBUS[16]; SUB = INSTRUCBUS[17]; TST = INSTRUCBUS[18]; STRCPY = INSTRUCBUS[19];
  //   JADR = INSTRUCBUS[20]; JMP = INSTRUCBUS[21]; JSR = INSTRUCBUS[22]; FETCH = PHASEFFBUS[0]; ADDR = PHASEFFBUS[1];
  //   EXEC = PHASEFFBUS[2]; INTR = PHASEFFBUS[3]; rst = in_1

  // Notes on the sheet:
  //   Operaciona jedinica
  //   Upravljacka jedinica
  //   contents of rom_1 (hex, n*v repeats v):
  //   800 1400 10403 1040c c413 6 d0c0 1 700
endmodule

module EXEC (
  input  in_1,
  input  in_2,
  input  in_3,
  input  [15:0] B,
  input  [31:0] INSTRUCBUS,
  input  [5:0] ADDRBUS,
  input  [15:0] PSW,
  input  [3:0] PHASEFFBUS,
  output [15:0] A,
  output [7:0] ALU,
  output [14:0] CMEMBUS,
  output [9:0] CFFBUS,
  output [19:0] CREGBUS,
  output [5:0] CPSW,
  output rdMEM,
  output wrMEM
);

  wire and_1_out, and_2_out, and_3_out, and_4_out, and_5_out, brcnd, brimmed, brnotbrorjmp, brnotEXEC,
       brnotFCBUS, bropr, brorjmp, brregdir, bruncnd, clEXEC, clPSWSTART, decSP, incA, incMAR, incSP, ldA,
       ldB, ldDR, ldDWH, ldDWL, ldMAR, ldMDR, ldN, ldPC, ldSTAR, ldSTBR, ldV, ldZ, mp2_6b_1_p2, mp2_6b_1_p3,
       mp2_6b_1_p4, mp8_16b_1_p4, mp8_16b_1_p6, mxA0, mxB1, mxMAR1, mxMDR0, mxMDR1, mxPC1, not_1_out,
       not_2_out, not_4_out, not_5_out, not_6_out, rdMEM_t, reg6_inc_ld_1_p4, reg6_inc_ld_1_p5,
       reg6_inc_ld_1_p6, stINTR, undriven, wrMEM_t;
  wire [15:0] MDR7__0, SUB15__0;
  wire [30:28] dc3_8_1_p1;

  // MP8_16b mp8_16b_1: pin names not known; wires that end beside it: mxA0, B, SUB15__0, mp8_16b_1_p4, mp8_16b_1_p4, mp8_16b_1_p6, MDR7__0, 1'b1
  not not_1 (not_1_out, in_1);
  // Probe on mp8_16b_1_p6
  // REG16m_INC_LD reg16m_inc_ld_1: pin names not known; wires that end beside it: in_2, not_1_out, mp8_16b_1_p6, A, ldA, incA, 1'b0
  // Probe on A
  not not_2 (not_2_out, in_1);
  // DC3_8 dc3_8_1: pin names not known; wires that end beside it: dc3_8_1_p1, 1'b1, bruncnd, brnotEXEC, brimmed, brregdir, brnotbrorjmp, brnotFCBUS, bropr
  // MP2_6b mp2_6b_1: pin names not known; wires that end beside it: bropr, mp2_6b_1_p2, mp2_6b_1_p3, mp2_6b_1_p4, 1'b1
  // REG6_INC_LD reg6_inc_ld_1: pin names not known; wires that end beside it: in_2, not_2_out, mp2_6b_1_p3, reg6_inc_ld_1_p4, reg6_inc_ld_1_p5, reg6_inc_ld_1_p6
  not not_3 (reg6_inc_ld_1_p6, reg6_inc_ld_1_p5);
  // ROM64x37 rom64x37_1: pin names not known; wires that end beside it: reg6_inc_ld_1_p4, 1'b1, mp2_6b_1_p2, {dc3_8_1_p1, clEXEC, stINTR, mxMDR1, mxB1, ldB, rdMEM_t, ldMAR, incMAR, ldSTBR, ldSTAR, mxPC1, ldDWH, ldDWL, incSP, decSP, mxMAR1, clPSWSTART, ldPC, mxA0, incA, ldDR, mxMDR0, wrMEM_t, ldMDR, ldV, ldZ, ldN, ldA}
  // KMOPR kmopr_1: pin names not known; wires that end beside it: INSTRUCBUS[14], INSTRUCBUS[15], INSTRUCBUS[16], INSTRUCBUS[17], INSTRUCBUS[21], INSTRUCBUS[0], mp2_6b_1_p4, INSTRUCBUS[5], INSTRUCBUS[6], INSTRUCBUS[20], INSTRUCBUS[7], INSTRUCBUS[9]
  or or_1 (reg6_inc_ld_1_p5, bruncnd, brcnd, bropr);
  // SUB16 sub16_1: pin names not known; wires that end beside it: A, SUB15__0, B, 1'b0
  // Probe on B
  // Probe on SUB15__0
  not not_4 (not_4_out, PHASEFFBUS[2]);
  not not_5 (not_5_out, brorjmp);
  not not_6 (not_6_out, in_3);
  and and_1 (and_1_out, not_4_out, brnotEXEC);
  and and_2 (and_2_out, ADDRBUS[0], brimmed);
  and and_3 (and_3_out, ADDRBUS[2], brregdir);
  and and_4 (and_4_out, not_5_out, brnotbrorjmp);
  and and_5 (and_5_out, not_6_out, brnotFCBUS);
  or or_2 (brcnd, and_1_out, and_2_out, and_3_out, and_4_out, and_5_out);
  assign CMEMBUS[0] = ldMAR ? 1'b1 : 1'bz;  // Controlled_Buffer controlled_buffer_1
  assign CMEMBUS[1] = incMAR ? 1'b1 : 1'bz;  // Controlled_Buffer controlled_buffer_2
  assign CMEMBUS[2] = ldMDR ? 1'b1 : 1'bz;  // Controlled_Buffer controlled_buffer_3
  assign CMEMBUS[3] = ldPC ? 1'b1 : 1'bz;  // Controlled_Buffer controlled_buffer_4
  assign CMEMBUS[6] = mxMAR1 ? 1'b1 : 1'bz;  // Controlled_Buffer controlled_buffer_5
  assign CMEMBUS[10] = mxMDR0 ? 1'b1 : 1'bz;  // Controlled_Buffer controlled_buffer_6
  assign CMEMBUS[11] = mxPC1 ? 1'b1 : 1'bz;  // Controlled_Buffer controlled_buffer_7
  Controlled_Buffer controlled_buffer_8 (.in(1'b1), .en(undriven));  // open: out
  assign CMEMBUS[9] = mxMDR1 ? 1'b1 : 1'bz;  // Controlled_Buffer controlled_buffer_9
  assign CREGBUS[4] = ldB ? 1'b1 : 1'bz;  // Controlled_Buffer controlled_buffer_10
  assign CREGBUS[6] = mxB1 ? 1'b1 : 1'bz;  // Controlled_Buffer controlled_buffer_11
  assign CREGBUS[7] = ldA ? 1'b1 : 1'bz;  // Controlled_Buffer controlled_buffer_12
  assign CREGBUS[8] = ldDR ? 1'b1 : 1'bz;  // Controlled_Buffer controlled_buffer_13
  assign CREGBUS[9] = incA ? 1'b1 : 1'bz;  // Controlled_Buffer controlled_buffer_14
  assign CREGBUS[10] = mxA0 ? 1'b1 : 1'bz;  // Controlled_Buffer controlled_buffer_15
  assign CREGBUS[11] = decSP ? 1'b1 : 1'bz;  // Controlled_Buffer controlled_buffer_16
  assign CREGBUS[12] = incSP ? 1'b1 : 1'bz;  // Controlled_Buffer controlled_buffer_17
  assign CREGBUS[13] = ldDWL ? 1'b1 : 1'bz;  // Controlled_Buffer controlled_buffer_18
  assign CREGBUS[14] = ldDWH ? 1'b1 : 1'bz;  // Controlled_Buffer controlled_buffer_19
  assign CREGBUS[15] = ldSTAR ? 1'b1 : 1'bz;  // Controlled_Buffer controlled_buffer_20
  assign CREGBUS[16] = ldSTBR ? 1'b1 : 1'bz;  // Controlled_Buffer controlled_buffer_21
  assign CREGBUS[17] = ldN ? 1'b1 : 1'bz;  // Controlled_Buffer controlled_buffer_22
  assign CREGBUS[18] = ldZ ? 1'b1 : 1'bz;  // Controlled_Buffer controlled_buffer_23
  assign CREGBUS[19] = ldV ? 1'b1 : 1'bz;  // Controlled_Buffer controlled_buffer_24
  assign rdMEM = rdMEM_t ? 1'b1 : 1'bz;  // Controlled_Buffer controlled_buffer_25
  assign wrMEM = wrMEM_t ? 1'b1 : 1'bz;  // Controlled_Buffer controlled_buffer_26
  assign CFFBUS[5] = clEXEC ? 1'b1 : 1'bz;  // Controlled_Buffer controlled_buffer_27
  assign CFFBUS[6] = stINTR ? 1'b1 : 1'bz;  // Controlled_Buffer controlled_buffer_28
  assign CFFBUS[8] = clPSWSTART ? 1'b1 : 1'bz;  // Controlled_Buffer controlled_buffer_29

  // Other names for the same wires on the sheet: A15__0[15:0] = A; immed = ADDRBUS[0]; memdir = ADDRBUS[1];
  //   regdir = ADDRBUS[2]; regind = ADDRBUS[3]; brpom = ADDRBUS[4]; bxpom = ADDRBUS[5]; ALU7__0[7:0] = ALU;
  //   B15__0[15:0] = B; CLK = in_2; FCBUS = in_3; HALT = INSTRUCBUS[0]; RTS = INSTRUCBUS[1]; RTI = INSTRUCBUS[2];
  //   INTE = INSTRUCBUS[3]; INTD = INSTRUCBUS[4]; PUSH = INSTRUCBUS[5]; POP = INSTRUCBUS[6]; STBR = INSTRUCBUS[7];
  //   STXR = INSTRUCBUS[8]; STAR = INSTRUCBUS[9]; BNEQ = INSTRUCBUS[10]; BOVF = INSTRUCBUS[11]; JNNG = INSTRUCBUS[12];
  //   JGRT = INSTRUCBUS[13]; LD = INSTRUCBUS[14]; ST = INSTRUCBUS[15]; INC = INSTRUCBUS[16]; SUB = INSTRUCBUS[17];
  //   TST = INSTRUCBUS[18]; STRCPY = INSTRUCBUS[19]; JADR = INSTRUCBUS[20]; JMP = INSTRUCBUS[21];
  //   JSR = INSTRUCBUS[22]; EXEC = PHASEFFBUS[2]; INTR = PHASEFFBUS[3]; rst = in_1

  // Notes on the sheet:
  //   Operaciona jedinica
  //   Upravljacka jedinica
  //   Akumulator
endmodule

module INTR (
  input  in_1,
  input  in_2,
  input  in_3,
  input  [3:0] PHASEFFBUS,
  input  [31:0] INSTRUCBUS,
  input  [15:0] PSW,
  input  [7:0] intr,
  input  [15:0] ACC,
  output [15:0] ADDIVTP,
  output [2:0] UEXT1__0,
  output inta,
  output [14:0] CMEMBUS,
  output [9:0] CFFBUS,
  output [19:0] CREGBUS,
  output rdMEM,
  output wrMEM
);

  wire and_2_out, and_3_out, and_4_out, brcnd, brnotFCBUS, brnotINTR, brnotprekid, bruncnd, clINTR, decSP,
       incMAR, incPC, ldDWH, ldDWL, ldMAR, ldMDR, ldPC, mxMAR0, mxMAR1, mxMAR2, mxMDR0, mxMDR1, mxMDR2,
       mxPC0, mxPC1, not_1_out, not_2_out, not_3_out, not_5_out, not_6_out, not_7_out, or_1_out, prekid,
       rdMEM_t, reg5_cl_inc_ld_1_p5, reg5_cl_inc_ld_1_p6, stFETCH, wrMEM_t;
  wire [2:0] dc3_8_1_p1, UEXT2__0;
  wire [3:1] IVTP15__0;
  wire [4:0] reg5_cl_inc_ld_1_p3, reg5_cl_inc_ld_1_p4;
  wire [15:0] IVTDSP15__0;

  and and_1 (prekid, or_1_out, PSW[15], not_2_out);
  not not_1 (not_1_out, in_1);
  // REG16_LD reg16_ld_1: pin names not known; wires that end beside it: in_2, not_1_out, {{12{1'b0}}, IVTP15__0, 1'b0}
  not not_2 (not_2_out, INSTRUCBUS[0]);
  or or_1 (or_1_out, intr[7], intr[6], intr[5], intr[4], intr[3], intr[2], intr[1], intr[0]);
  not not_3 (not_3_out, in_1);
  // REG5_CL_INC_LD reg5_cl_inc_ld_1: pin names not known; wires that end beside it: in_2, not_3_out, reg5_cl_inc_ld_1_p3, reg5_cl_inc_ld_1_p4, reg5_cl_inc_ld_1_p5, reg5_cl_inc_ld_1_p6
  // DC3_8 dc3_8_1: pin names not known; wires that end beside it: dc3_8_1_p1, 1'b1, bruncnd, brnotINTR, brnotprekid, brnotFCBUS
  not not_4 (reg5_cl_inc_ld_1_p6, reg5_cl_inc_ld_1_p5);
  or or_2 (reg5_cl_inc_ld_1_p5, bruncnd, brcnd);
  // CD8 cd8_1: pin names not known; wires that end beside it: intr[7], intr[6], intr[5], intr[4], intr[3], intr[2], intr[1], intr[0], 1'b1, UEXT2__0[2], UEXT2__0[1], UEXT2__0[0]
  ROM #(.addrWidth(5), .dataWidth(27)) rom_1 (
    .addr(reg5_cl_inc_ld_1_p4),
    .data({reg5_cl_inc_ld_1_p3, dc3_8_1_p1, clINTR, stFETCH, mxPC0, ldPC, ldDWH, ldDWL, incMAR, rdMEM_t, mxMAR2, inta, mxMDR2, mxMDR0, wrMEM_t, ldMDR, mxMDR1, decSP, ldMAR, mxMAR1, mxMAR0}));  // open: sel
  // REG3_LD reg3_ld_1: pin names not known; wires that end beside it: in_2, UEXT2__0, IVTP15__0, inta
  // ADD16 add16_1: pin names not known; wires that end beside it: {{12{1'b0}}, IVTP15__0, 1'b0}, ADDIVTP, IVTDSP15__0, 1'b0
  not not_5 (not_5_out, PHASEFFBUS[3]);
  not not_6 (not_6_out, prekid);
  not not_7 (not_7_out, in_3);
  and and_2 (and_2_out, not_5_out, brnotINTR);
  and and_3 (and_3_out, not_6_out, brnotprekid);
  and and_4 (and_4_out, not_7_out, brnotFCBUS);
  or or_3 (brcnd, and_2_out, and_3_out, and_4_out);
  assign CMEMBUS[0] = ldMAR ? 1'b1 : 1'bz;  // Controlled_Buffer controlled_buffer_1
  assign CMEMBUS[1] = incMAR ? 1'b1 : 1'bz;  // Controlled_Buffer controlled_buffer_2
  assign CMEMBUS[2] = ldMDR ? 1'b1 : 1'bz;  // Controlled_Buffer controlled_buffer_3
  assign CMEMBUS[3] = ldPC ? 1'b1 : 1'bz;  // Controlled_Buffer controlled_buffer_4
  Controlled_Buffer controlled_buffer_5 (.in(1'b1), .en(incPC));  // open: out
  assign CMEMBUS[5] = mxMAR2 ? 1'b1 : 1'bz;  // Controlled_Buffer controlled_buffer_6
  assign CMEMBUS[6] = mxMAR1 ? 1'b1 : 1'bz;  // Controlled_Buffer controlled_buffer_7
  assign CMEMBUS[7] = mxMAR0 ? 1'b1 : 1'bz;  // Controlled_Buffer controlled_buffer_8
  assign CMEMBUS[8] = mxMDR2 ? 1'b1 : 1'bz;  // Controlled_Buffer controlled_buffer_9
  assign CMEMBUS[9] = mxMDR1 ? 1'b1 : 1'bz;  // Controlled_Buffer controlled_buffer_10
  assign CMEMBUS[10] = mxMDR0 ? 1'b1 : 1'bz;  // Controlled_Buffer controlled_buffer_11
  Controlled_Buffer controlled_buffer_12 (.in(1'b1), .en(mxPC1));  // open: out
  assign CMEMBUS[12] = mxPC0 ? 1'b1 : 1'bz;  // Controlled_Buffer controlled_buffer_13
  assign CMEMBUS[13] = decSP ? 1'b1 : 1'bz;  // Controlled_Buffer controlled_buffer_14
  assign CFFBUS[0] = stFETCH ? 1'b1 : 1'bz;  // Controlled_Buffer controlled_buffer_15
  assign CFFBUS[7] = clINTR ? 1'b1 : 1'bz;  // Controlled_Buffer controlled_buffer_16
  assign CREGBUS[13] = ldDWL ? 1'b1 : 1'bz;  // Controlled_Buffer controlled_buffer_17
  assign CREGBUS[14] = ldDWH ? 1'b1 : 1'bz;  // Controlled_Buffer controlled_buffer_18
  assign rdMEM = rdMEM_t ? 1'b1 : 1'bz;  // Controlled_Buffer controlled_buffer_19
  assign wrMEM = wrMEM_t ? 1'b1 : 1'bz;  // Controlled_Buffer controlled_buffer_20

  // Other names for the same wires on the sheet: ldBR = inta; ADDIVTP15__0[15:0] = ADDIVTP; CLK = in_2; FCBUS = in_3;
  //   HALT = INSTRUCBUS[0]; intr7__0[7:0] = intr; INTR_t = PHASEFFBUS[3]; PSWI = PSW[15]; rst = in_1

  // Notes on the sheet:
  //   Operaciona jedinica
  //   Upravljacka jedinica
  //   contents of rom_1 (hex, n*v repeats v):
  //   100000 4180000 12e e00040 1ae 1600040 13e 1e00040 1be 2600040 200 2e00820 3000 3600820 4000 18000
  //   60000
endmodule

module RAM (
  input  [15:0] in_1,
  input  in_2,
  input  [7:0] in_3,
  input  in_4,
  input  in_5,
  input  in_6,
  output [7:0] out_7,
  output out_8
);

  wire and_1_out, and_2_out, CNT0, LDCNT, not_1_out, notCNT0, or_1_out, reg4_ld_sl_sr_1_p6, rsff_2_p4,
       rsff_2_p5, rsff_3_p4, sl;
  wire [3:0] CNT, LFSR;

  // RSFF rsff_1: pin names not known; wires that end beside it: 1'b0, in_2, in_6, sl
  or or_1 (or_1_out, in_4, in_5);
  // REG4_LD_SL_SR reg4_ld_sl_sr_1: pin names not known; wires that end beside it: 1'b0, 1'b0, in_2, 4'b1111, LFSR, reg4_ld_sl_sr_1_p6, sl, in_6
  // RisingEdge risingedge_1: pin names not known; wires that end beside it: or_1_out, in_2, LDCNT
  // MEM64Kx8 mem64kx8_1: pin names not known; wires that end beside it: in_1, 1'b1, in_2, in_3, out_7, in_4
  xor xor_1 (reg4_ld_sl_sr_1_p6, LFSR[2], LFSR[3]);
  and and_1 (and_1_out, CNT0, not_1_out);
  not not_1 (not_1_out, LDCNT);
  // RSFF rsff_2: pin names not known; wires that end beside it: and_1_out, in_2, LDCNT, rsff_2_p4, rsff_2_p5
  not not_2 (rsff_2_p4, in_6);
  and and_2 (and_2_out, rsff_2_p5, CNT0);
  // REG4m_DEC_LD reg4m_dec_ld_1: pin names not known; wires that end beside it: in_2, LFSR, CNT, LDCNT, notCNT0, notCNT0
  or or_2 (notCNT0, CNT[0], CNT[1], CNT[2], CNT[3]);
  // RSFF rsff_3: pin names not known; wires that end beside it: out_8, in_2, and_2_out, rsff_3_p4, out_8
  not not_3 (rsff_3_p4, in_6);
  not not_4 (CNT0, notCNT0);

  // Other names for the same wires on the sheet: ADR[15:0] = in_1; CLK = in_2; DIN[7:0] = in_3; DOUT[7:0] = out_7;
  //   fc = out_8; RDMEM = in_5; rst = in_6; WRMEM = in_4

  // Notes on the sheet:
  //   Random broj predstavlja vreme pristupa memoriji
  //   Brojac za generisanje random broja 
  //   Jedinica za generisanje function complete (fc) signala
  //   Brojac za dekrementiranje random broja
endmodule
